// Digital circuit ALU_8bit.dig as structural Verilog
module ALU_8bit (
  input  [7:0] A,
  input  [7:0] B,
  output [7:0] Y,
  output EQ,
  output GT,
  output LT
);

  wire [3:0] ALU_Op;
  wire [7:0] add_1_s, and_1_out, barrelshifter_1_out, barrelshifter_2_out, not_1_out, or_1_out, sub_1_s,
       xor_1_out;

  Add #(.Bits(8)) add_1 (.a(A), .b(B), .s(add_1_s));  // open: c_i, c_o
  Sub #(.Bits(8)) sub_1 (.a(A), .b(B), .s(sub_1_s));  // open: c_i, c_o
  assign and_1_out = A & B;  // And and_1, 8 bits wide
  assign or_1_out = A | B;  // Or or_1, 8 bits wide
  assign xor_1_out = A ^ B;  // XOr xor_1, 8 bits wide
  assign not_1_out = ~A;  // Not not_1, 8 bits wide
  BarrelShifter #(.Bits(8), .direction("right")) barrelshifter_1 (.in(A), .shift(B), .out(barrelshifter_1_out));
  BarrelShifter #(.Bits(8), .barrelSigned("true"), .direction("right")) barrelshifter_2 (
    .in(A), .shift(B), .out(barrelshifter_2_out));
  Multiplexer #(.Bits(8), .Selector_Bits(4)) multiplexer_1 (
    .sel(ALU_Op), .in_0(add_1_s), .in_1(sub_1_s), .in_2(and_1_out), .in_3(or_1_out), .in_4(xor_1_out),
    .in_5(not_1_out), .in_6(barrelshifter_1_out), .in_7(barrelshifter_2_out), .in_8({8{1'b0}}),
    .in_9({8{1'b0}}), .in_10({8{1'b0}}), .in_11({8{1'b0}}), .in_12({8{1'b0}}), .in_13({8{1'b0}}),
    .in_14({8{1'b0}}), .in_15({8{1'b0}}), .out(Y));
  Comparator #(.Bits(8)) comparator_1 (.a(A), .b(B), .gt(GT), .eq(EQ), .lt(LT));

  // Other names for the same wires on the sheet: ALU_Result[7:0] = Y
endmodule
