// Digital circuit Card7.dig as structural Verilog
module Card7 (
  input  [7:0] M,
  input  [7:0] N,
  input  [13:0] progIn,
  input  reset,
  input  progLoad,
  input  start,
  input  result,
  input  clk,
  output valid,
  output done,
  output [7:0] \output 
);

  wire ALU_Source_B, and_1_out, and_2_out, and_3_out, and_4_out, decoder_1_out_0, decoder_1_out_1,
       decoder_1_out_2, decoder_1_out_3, EQ, Flag_Write, GT, Input_Select, IR_Write, LT, Mem_Addr_Source,
       Mem_Read, Mem_Write, or_1_out, or_2_out, PC_Write, Q, Reg_Write;
  wire [1:0] A_r1, A_r2, A_w, PC_Source, Reg_Source;
  wire [7:0] ALU_Result, D_r2_OUT, Mem_Read_Data, Memory_Address_Bus, Memory_Address_MUX, multiplexer_1_out,
       multiplexer_6_out, multiplexer_7_out, Operand_Extended, PC_plus_1_Result, PC_Register;
  wire [7:1] undriven;
  wire [13:0] pRAM_d1;
  wire [15:0] D_r1, D_r2, Reg_A, Reg_B, Reg_C, Reg_D;

  or or_1 (or_1_out, Mem_Read, progLoad);
  RAMDualAccess #(.AddrBits(8), .Bits(14)) pRAM (
    .str(reset), .C(clk), .ld(or_1_out), .A1(PC_plus_1_Result), .Din1(progIn), .D1(pRAM_d1));  // open: A2, D2
  or or_2 (or_2_out, Mem_Read, Mem_Write);
  Register #(.Bits(8)) PC (.D(multiplexer_1_out), .C(clk), .en(PC_Write), .Q(Memory_Address_MUX));
  Register #(.Bits(14)) IR (.D(pRAM_d1), .C(IR_Write), .en(clk), .Q({A_r2, A_r1, A_w, PC_plus_1_Result}));
  Add #(.Bits(8)) add_1 (.a(Memory_Address_MUX), .b({undriven, 1'b1}), .s(PC_plus_1_Result));  // open: c_i, c_o
  RAMDualAccess #(.AddrBits(8), .Bits(8)) rRAM (
    .str(reset), .C(clk), .ld(or_2_out), .A1(PC_plus_1_Result), .Din1(D_r2_OUT), .D1(Mem_Read_Data));  // open: A2, D2
  Multiplexer #(.Selector_Bits(2), .Bits(8)) multiplexer_1 (
    .sel(PC_Source), .in_0(PC_plus_1_Result), .in_1(Operand_Extended), .out(multiplexer_1_out));  // open: in_2, in_3
  Multiplexer #(.Selector_Bits(2), .Bits(16)) multiplexer_2 (
    .sel(A_r1), .in_0(Reg_A), .in_1(Reg_B), .in_2(Reg_C), .in_3(Reg_D), .out(D_r1));
  Multiplexer #(.Selector_Bits(2), .Bits(16)) multiplexer_3 (
    .sel(A_r2), .in_0(Reg_A), .in_1(Reg_B), .in_2(Reg_C), .in_3(Reg_D), .out(D_r2));
  Register #(.Bits(8)) u_PC_Register (.D(multiplexer_1_out), .C(clk), .en(PC_Write), .Q(PC_Register));
  Seven_Seg_Hex seven_seg_hex_1 (.d(\output [7:4]), .dp(1'b0));
  Multiplexer #(.Bits(8)) multiplexer_4 (.sel(ALU_Source_B), .in_0(D_r2[7:0]), .in_1(PC_plus_1_Result), .out(D_r2_OUT));
  Multiplexer #(.Bits(8)) multiplexer_5 (
    .sel(Mem_Addr_Source), .in_0(PC_Register), .in_1(ALU_Result), .out(Memory_Address_Bus));
  Decoder #(.Selector_Bits(2)) decoder_1 (
    .sel(A_w), .out_0(decoder_1_out_0), .out_1(decoder_1_out_1), .out_2(decoder_1_out_2),
    .out_3(decoder_1_out_3));
  Seven_Seg_Hex seven_seg_hex_2 (.d(\output [3:0]), .dp(1'b0));
  Multiplexer #(.Bits(8)) multiplexer_6 (.sel(Input_Select), .in_0(M), .in_1(N), .out(multiplexer_6_out));
  and and_1 (and_1_out, Reg_Write, decoder_1_out_0);
  and and_2 (and_2_out, Reg_Write, decoder_1_out_1);
  and and_3 (and_3_out, Reg_Write, decoder_1_out_2);
  and and_4 (and_4_out, Reg_Write, decoder_1_out_3);
  Register EQ_Reg (.D(EQ), .C(clk), .en(Flag_Write), .Q(Q));
  Register GT_Reg (.D(GT), .C(clk), .en(Flag_Write), .Q(Q));
  Register LT_Reg (.D(LT), .C(clk), .en(Flag_Write), .Q(Q));
  Multiplexer #(.Selector_Bits(2), .Bits(8)) multiplexer_7 (
    .sel(Reg_Source), .in_0(ALU_Result), .in_1(Mem_Read_Data), .in_2(Operand_Extended),
    .in_3(multiplexer_6_out), .out(multiplexer_7_out));
  Register #(.Bits(8)) u_Reg_A (.D(multiplexer_7_out), .C(clk), .en(and_1_out), .Q(Reg_A[7:0]));
  Register #(.Bits(8)) u_Reg_B (.D(multiplexer_7_out), .C(clk), .en(and_2_out), .Q(Reg_B[7:0]));
  Register #(.Bits(8)) u_Reg_C (.D(multiplexer_7_out), .C(clk), .en(and_3_out), .Q(Reg_C[7:0]));
  Register #(.Bits(8)) u_Reg_D (.D(multiplexer_7_out), .C(clk), .en(and_4_out), .Q(Reg_D[7:0]));
  // Pins of 8 and 16 bits meet at Reg_A
  // Pins of 8 and 16 bits meet at Reg_B
  // Pins of 8 and 16 bits meet at Reg_D
  // Pins of 8 and 16 bits meet at Reg_C
  // Pins of 8 and 16 bits meet at D_r2
  // Pins of 1 and 8 bits meet at {undriven, 1'b1}
endmodule

/* Test case 01_P01T01:
M N progIn reset progLoad start result clk valid done output
0 0      0     0        0     0      0   0     x    x      x
0 0      0     0        0     0      0   1     x    x      x
0 0      0     1        0     0      0   0     x    x      x
0 0      0     1        0     0      0   1     0    0      x
0 0      0     0        0     0      0   0     0    0      x
0 0      0     0        0     0      0   1     0    0      x
0 0      0     0        0     0      0   0     0    0      x
0 0      0     0        0     0      0   1     0    0      x
0 0      0     0        0     0      0   0     0    0      x
0 0      0     0        0     0      0   1     0    0      x
0 0      0     0        0     0      0   0     0    0      x
0 0      0     0        0     0      0   1     0    0      x
0 0      0     0        0     0      0   0     0    0      x
0 0      0     0        0     0      0   1     0    0      x
0 0      0     0        0     0      0   0     0    0      x
0 0      0     0        0     0      0   1     0    0      x
0 0      0     0        0     0      0   0     0    0      x
0 0      0     0        0     0      0   1     0    0      x
0 0      0     0        0     0      0   0     0    0      x
0 0      0     0        0     0      0   1     0    0      x
0 0      0     0        0     0      0   0     0    0      x
0 0      0     0        0     0      0   1     0    0      x
0 0      0     0        0     0      0   0     0    0      x
0 0      0     0        0     0      0   1     0    0      x
0 0      0     0        0     0      0   0     0    0      x
0 0      0     0        0     0      0   1     0    0      x
0 0      0     0        0     0      0   0     0    0      x
0 0      0     0        0     0      0   1     0    0      x
0 0      0     0        0     0      0   0     0    0      x
0 0      0     0        0     0      0   1     0    0      x
0 0      0     0        0     0      0   0     0    0      x
0 0      0     0        0     0      0   1     0    0      x
0 0      0     0        0     0      0   0     0    0      x
0 0      0     0        0     0      0   1     0    0      x
0 0      0     0        0     0      0   0     0    0      x
0 0      0     0        0     0      0   1     0    0      x
0 0      0     0        0     0      0   0     0    0      x
0 0      0     0        0     0      0   1     0    0      x
0 0      0     0        0     0      0   0     0    0      x
0 0      0     0        0     0      0   1     0    0      x
0 0      0     0        0     0      0   0     0    0      x
0 0      0     0        0     0      0   1     0    0      x
0 0    271     0        1     0      0   0     0    0      x
0 0    271     0        1     0      0   1     0    0      x
0 0    565     0        1     0      0   0     0    0      x
0 0    565     0        1     0      0   1     0    0      x
0 0   8192     0        1     0      0   0     0    0      x
0 0   8192     0        1     0      0   1     0    0      x
0 0   4355     0        1     0      0   0     0    0      x
0 0   4355     0        1     0      0   1     0    0      x
0 0  16128     0        1     0      0   0     0    0      x
0 0  16128     0        1     0      0   1     0    0      x
0 0      0     0        0     1      0   0     0    0      x
0 0      0     0        0     1      0   1     0    0      x
0 0      0     0        0     0      0   0     x    0      x
0 0      0     0        0     0      0   1     x    0      x
0 0      0     0        0     0      0   0     x    0      x
0 0      0     0        0     0      0   1     x    0      x
0 0      0     0        0     0      0   0     x    0      x
0 0      0     0        0     0      0   1     x    0      x
0 0      0     0        0     0      0   0     x    0      x
0 0      0     0        0     0      0   1     x    0      x
0 0      0     0        0     0      0   0     x    0      x
0 0      0     0        0     0      0   1     x    0      x
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*/

/* Test case 02_P01T02:
M N progIn reset progLoad start result clk valid done output
0 0      0     0        0     0      0   0     x    x      x
0 0      0     0        0     0      0   1     x    x      x
0 0      0     1        0     0      0   0     x    x      x
0 0      0     1        0     0      0   1     0    0      x
0 0      0     0        0     0      0   0     0    0      x
0 0      0     0        0     0      0   1     0    0      x
0 0      0     0        0     0      0   0     0    0      x
0 0      0     0        0     0      0   1     0    0      x
0 0      0     0        0     0      0   0     0    0      x
0 0      0     0        0     0      0   1     0    0      x
0 0      0     0        0     0      0   0     0    0      x
0 0      0     0        0     0      0   1     0    0      x
0 0      0     0        0     0      0   0     0    0      x
0 0      0     0        0     0      0   1     0    0      x
0 0      0     0        0     0      0   0     0    0      x
0 0      0     0        0     0      0   1     0    0      x
0 0      0     0        0     0      0   0     0    0      x
0 0      0     0        0     0      0   1     0    0      x
0 0      0     0        0     0      0   0     0    0      x
0 0      0     0        0     0      0   1     0    0      x
0 0      0     0        0     0      0   0     0    0      x
0 0      0     0        0     0      0   1     0    0      x
0 0      0     0        0     0      0   0     0    0      x
0 0      0     0        0     0      0   1     0    0      x
0 0      0     0        0     0      0   0     0    0      x
0 0      0     0        0     0      0   1     0    0      x
0 0      0     0        0     0      0   0     0    0      x
0 0      0     0        0     0      0   1     0    0      x
0 0      0     0        0     0      0   0     0    0      x
0 0      0     0        0     0      0   1     0    0      x
0 0      0     0        0     0      0   0     0    0      x
0 0      0     0        0     0      0   1     0    0      x
0 0      0     0        0     0      0   0     0    0      x
0 0      0     0        0     0      0   1     0    0      x
0 0      0     0        0     0      0   0     0    0      x
0 0      0     0        0     0      0   1     0    0      x
0 0      0     0        0     0      0   0     0    0      x
0 0      0     0        0     0      0   1     0    0      x
0 0      0     0        0     0      0   0     0    0      x
0 0      0     0        0     0      0   1     0    0      x
0 0      0     0        0     0      0   0     0    0      x
0 0      0     0        0     0      0   1     0    0      x
0 0    271     0        1     0      0   0     0    0      x
0 0    271     0        1     0      0   1     0    0      x
0 0    565     0        1     0      0   0     0    0      x
0 0    565     0        1     0      0   1     0    0      x
0 0   8192     0        1     0      0   0     0    0      x
0 0   8192     0        1     0      0   1     0    0      x
0 0   4355     0        1     0      0   0     0    0      x
0 0   4355     0        1     0      0   1     0    0      x
0 0  16128     0        1     0      0   0     0    0      x
0 0  16128     0        1     0      0   1     0    0      x
0 0      0     0        0     1      0   0     0    0      x
0 0      0     0        0     1      0   1     0    0      x
0 0      0     0        0     0      0   0     x    0      x
0 0      0     0        0     0      0   1     x    0      x
0 0      0     0        0     0      0   0     x    0      x
0 0      0     0        0     0      0   1     x    0      x
0 0      0     0        0     0      0   0     x    0      x
0 0      0     0        0     0      0   1     x    0      x
0 0      0     0        0     0      0   0     x    0      x
0 0      0     0        0     0      0   1     x    0      x
0 0      0     0        0     0      0   0     x    0      x
0 0      0     0        0     0      0   1     x    0      x
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*/

/* Test case 03_P02T01:
M N progIn reset progLoad start result clk valid done output
0 0      0     0        0     0      0   0     x    x      x
0 0      0     0        0     0      0   1     x    x      x
0 0      0     1        0     0      0   0     x    x      x
0 0      0     1        0     0      0   1     0    0      x
0 0      0     0        0     0      0   0     0    0      x
0 0      0     0        0     0      0   1     0    0      x
0 0      0     0        0     0      0   0     0    0      x
0 0      0     0        0     0      0   1     0    0      x
0 0      0     0        0     0      0   0     0    0      x
0 0      0     0        0     0      0   1     0    0      x
0 0      0     0        0     0      0   0     0    0      x
0 0      0     0        0     0      0   1     0    0      x
0 0      0     0        0     0      0   0     0    0      x
0 0      0     0        0     0      0   1     0    0      x
0 0      0     0        0     0      0   0     0    0      x
0 0      0     0        0     0      0   1     0    0      x
0 0      0     0        0     0      0   0     0    0      x
0 0      0     0        0     0      0   1     0    0      x
0 0      0     0        0     0      0   0     0    0      x
0 0      0     0        0     0      0   1     0    0      x
0 0      0     0        0     0      0   0     0    0      x
0 0      0     0        0     0      0   1     0    0      x
0 0      0     0        0     0      0   0     0    0      x
0 0      0     0        0     0      0   1     0    0      x
0 0      0     0        0     0      0   0     0    0      x
0 0      0     0        0     0      0   1     0    0      x
0 0      0     0        0     0      0   0     0    0      x
0 0      0     0        0     0      0   1     0    0      x
0 0      0     0        0     0      0   0     0    0      x
0 0      0     0        0     0      0   1     0    0      x
0 0      0     0        0     0      0   0     0    0      x
0 0      0     0        0     0      0   1     0    0      x
0 0      0     0        0     0      0   0     0    0      x
0 0      0     0        0     0      0   1     0    0      x
0 0      0     0        0     0      0   0     0    0      x
0 0      0     0        0     0      0   1     0    0      x
0 0      0     0        0     0      0   0     0    0      x
0 0      0     0        0     0      0   1     0    0      x
0 0      0     0        0     0      0   0     0    0      x
0 0      0     0        0     0      0   1     0    0      x
0 0      0     0        0     0      0   0     0    0      x
0 0      0     0        0     0      0   1     0    0      x
0 0    271     0        1     0      0   0     0    0      x
0 0    271     0        1     0      0   1     0    0      x
0 0    566     0        1     0      0   0     0    0      x
0 0    566     0        1     0      0   1     0    0      x
0 0  12288     0        1     0      0   0     0    0      x
0 0  12288     0        1     0      0   1     0    0      x
0 0   5135     0        1     0      0   0     0    0      x
0 0   5135     0        1     0      0   1     0    0      x
0 0   5646     0        1     0      0   0     0    0      x
0 0   5646     0        1     0      0   1     0    0      x
0 0   5392     0        1     0      0   0     0    0      x
0 0   5392     0        1     0      0   1     0    0      x
0 0  16128     0        1     0      0   0     0    0      x
0 0  16128     0        1     0      0   1     0    0      x
0 0      0     0        1     0      0   0     0    0      x
0 0      0     0        1     0      0   1     0    0      x
0 0      0     0        1     0      0   0     0    0      x
0 0      0     0        1     0      0   1     0    0      x
0 0      0     0        1     0      0   0     0    0      x
0 0      0     0        1     0      0   1     0    0      x
0 0      0     0        1     0      0   0     0    0      x
0 0      0     0        1     0      0   1     0    0      x
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*/
