// Digital circuit Card8fix.dig as structural Verilog
module Card8fix (
  input  PC_Write,
  input  [13:0] IR_In,
  input  IR_Write,
  input  [1:0] Write_Address,
  input  Reg_Write,
  input  [1:0] Read_Address,
  input  [7:0] M,
  input  [7:0] N,
  input  [13:0] progIn,
  input  reset,
  input  progLoad,
  input  start,
  input  result,
  input  clk,
  input  [1:0] ALU_Op,
  input  Mem_Write,
  input  Mem_Read,
  input  PC_Source,
  input  ALU_Source_B,
  input  [1:0] Reg_Source,
  input  Mem_Addr_Source,
  input  ALU_Temp_A_Write,
  input  [7:0] Mem_Addr_MUX,
  input  Input_Select,
  output [7:0] out_2,
  output [13:0] IR_Out,
  output [7:0] Read_Data,
  output valid,
  output done,
  output [7:0] \output ,
  output [7:0] accA,
  output [7:0] accB,
  output [7:0] ALU_Result
);

  wire and_2_out, and_3_out, and_4_out, and_5_out, decoder_1_out_0, decoder_1_out_1, decoder_1_out_2,
       decoder_1_out_3, EQ, GT, LT, or_2_out, or_3_out, or_4_out, or_5_out, or_6_out;
  wire [7:0] accC_q, accD_q, add_1_s, add_2_s, ALU_Input_A, ALU_Input_B, and_1_out, EQout, GTout,
       Input_MUX_Out, LTout, Mem_Addr_MUX_Out, Mem_Read_Data, multiplexer_3_out, or_1_out, sub_1_s,
       Write_Data;
  wire [13:0] pRAM_d;

  Register #(.Bits(8)) register_1 (.D(Read_Data), .C(clk), .en(ALU_Temp_A_Write), .Q(ALU_Input_A));
  Multiplexer #(.Bits(8)) multiplexer_1 (.sel(ALU_Source_B), .in_0(Read_Data), .in_1(IR_Out[7:0]), .out(ALU_Input_B));
  Add #(.Bits(8)) add_1 (.a(ALU_Input_A), .b(ALU_Input_B), .c_i(1'b0), .s(add_1_s));  // open: c_o
  Sub #(.Bits(8)) sub_1 (.a(ALU_Input_A), .b(ALU_Input_B), .c_i(1'b0), .s(sub_1_s));  // open: c_o
  assign and_1_out = ALU_Input_A & ALU_Input_B;  // And and_1, 8 bits wide
  assign or_1_out = ALU_Input_A | ALU_Input_B;  // Or or_1, 8 bits wide
  Comparator #(.Bits(8)) comparator_1 (.a(ALU_Input_A), .b(ALU_Input_B), .gt(GT), .eq(EQ), .lt(LT));
  Multiplexer #(.Selector_Bits(2), .Bits(8)) multiplexer_2 (
    .sel(ALU_Op), .in_0(add_1_s), .in_1(sub_1_s), .in_2(and_1_out), .in_3(or_1_out), .out(ALU_Result));
  Add #(.Bits(8)) add_2 (.a(out_2), .b(8'h1), .c_i(1'b0), .s(add_2_s));  // open: c_o
  or or_2 (or_2_out, reset, GT);
  or or_3 (or_3_out, reset, EQ);
  or or_4 (or_4_out, reset, LT);
  Multiplexer #(.Bits(8)) multiplexer_3 (.sel(PC_Source), .in_0(add_2_s), .in_1(IR_Out[7:0]), .out(multiplexer_3_out));
  Register #(.Bits(8)) u_GT (.D(ALU_Result), .C(clk), .en(or_2_out), .Q(GTout));
  Register #(.Bits(8)) u_EQ (.D(ALU_Result), .C(clk), .en(or_3_out), .Q(EQout));
  Register #(.Bits(8)) u_LT (.D(ALU_Result), .C(clk), .en(or_4_out), .Q(LTout));
  Register #(.Bits(8)) PC_Reg (.D(multiplexer_3_out), .C(clk), .en(PC_Write), .Q(out_2));
  Multiplexer #(.Bits(8)) multiplexer_4 (.sel(result), .in_0({8{1'b0}}), .in_1(Mem_Read_Data), .out(\output ));
  or or_5 (or_5_out, Mem_Read, Mem_Write);
  or or_6 (or_6_out, Mem_Read, progLoad);
  Decoder #(.Selector_Bits(2)) decoder_1 (
    .sel(Write_Address), .out_0(decoder_1_out_0), .out_1(decoder_1_out_1), .out_2(decoder_1_out_2),
    .out_3(decoder_1_out_3));
  RAMDualPort #(.AddrBits(8), .Bits(8)) rRAM (
    .A(Mem_Addr_MUX_Out), .Din(Read_Data), .str(Mem_Write), .C(clk), .ld(or_5_out), .D(Mem_Read_Data));
  RAMDualPort #(.AddrBits(8), .Bits(14)) pRAM (
    .A(Mem_Addr_MUX), .Din(progIn), .str(reset), .C(clk), .ld(or_6_out), .D(pRAM_d));
  Seven_Seg_Hex seven_seg_hex_1 (.d(\output [7:4]), .dp(1'b0));
  and and_2 (and_2_out, Reg_Write, decoder_1_out_0);
  and and_3 (and_3_out, Reg_Write, decoder_1_out_1);
  and and_4 (and_4_out, Reg_Write, decoder_1_out_2);
  and and_5 (and_5_out, Reg_Write, decoder_1_out_3);
  Seven_Seg_Hex seven_seg_hex_2 (.d(\output [3:0]), .dp(1'b0));
  Register #(.Bits(14)) IR_reg (.D(pRAM_d), .C(clk), .en(IR_Write), .Q(IR_Out));
  Register #(.Bits(8)) u_accA (.D(Write_Data), .C(clk), .en(and_2_out), .Q(accA));
  Register #(.Bits(8)) u_accB (.D(Write_Data), .C(clk), .en(and_3_out), .Q(accB));
  Register #(.Bits(8)) accC (.D(Write_Data), .C(clk), .en(and_4_out), .Q(accC_q));
  Register #(.Bits(8)) accD (.D(Write_Data), .C(clk), .en(and_5_out), .Q(accD_q));
  Multiplexer #(.Selector_Bits(2), .Bits(8)) multiplexer_5 (
    .sel(Read_Address), .in_0(accA), .in_1(accB), .in_2(accC_q), .in_3(accD_q), .out(Read_Data));
  Multiplexer #(.Bits(8)) multiplexer_6 (
    .sel(Mem_Addr_Source), .in_0(out_2), .in_1(ALU_Result), .out(Mem_Addr_MUX_Out));
  Multiplexer #(.Bits(8)) multiplexer_7 (.sel(Input_Select), .in_0(M), .in_1(N), .out(Input_MUX_Out));
  Multiplexer #(.Selector_Bits(2), .Bits(8)) multiplexer_8 (
    .sel(Reg_Source), .in_0(ALU_Result), .in_1(Mem_Read_Data), .in_2(IR_Out[7:0]), .in_3(Input_MUX_Out),
    .out(Write_Data));

  assign done = 1'b0;
  assign valid = 1'b0;

  // Other names for the same wires on the sheet: Operand[7:0] = IR_Out[7:0]; Opcode[5:0] = IR_Out[13:8];
  //   PCout[7:0] = out_2
endmodule

/* Test case 01_P01T01:
M N progIn reset progLoad start result clk valid done output
0 0      0     0        0     0      0   0     x    x      x
0 0      0     0        0     0      0   1     x    x      x
0 0      0     1        0     0      0   0     x    x      x
0 0      0     1        0     0      0   1     0    0      x
0 0      0     0        0     0      0   0     0    0      x
0 0      0     0        0     0      0   1     0    0      x
0 0      0     0        0     0      0   0     0    0      x
0 0      0     0        0     0      0   1     0    0      x
0 0      0     0        0     0      0   0     0    0      x
0 0      0     0        0     0      0   1     0    0      x
0 0      0     0        0     0      0   0     0    0      x
0 0      0     0        0     0      0   1     0    0      x
0 0      0     0        0     0      0   0     0    0      x
0 0      0     0        0     0      0   1     0    0      x
0 0      0     0        0     0      0   0     0    0      x
0 0      0     0        0     0      0   1     0    0      x
0 0      0     0        0     0      0   0     0    0      x
0 0      0     0        0     0      0   1     0    0      x
0 0      0     0        0     0      0   0     0    0      x
0 0      0     0        0     0      0   1     0    0      x
0 0      0     0        0     0      0   0     0    0      x
0 0      0     0        0     0      0   1     0    0      x
0 0      0     0        0     0      0   0     0    0      x
0 0      0     0        0     0      0   1     0    0      x
0 0      0     0        0     0      0   0     0    0      x
0 0      0     0        0     0      0   1     0    0      x
0 0      0     0        0     0      0   0     0    0      x
0 0      0     0        0     0      0   1     0    0      x
0 0      0     0        0     0      0   0     0    0      x
0 0      0     0        0     0      0   1     0    0      x
0 0      0     0        0     0      0   0     0    0      x
0 0      0     0        0     0      0   1     0    0      x
0 0      0     0        0     0      0   0     0    0      x
0 0      0     0        0     0      0   1     0    0      x
0 0      0     0        0     0      0   0     0    0      x
0 0      0     0        0     0      0   1     0    0      x
0 0      0     0        0     0      0   0     0    0      x
0 0      0     0        0     0      0   1     0    0      x
0 0      0     0        0     0      0   0     0    0      x
0 0      0     0        0     0      0   1     0    0      x
0 0      0     0        0     0      0   0     0    0      x
0 0      0     0        0     0      0   1     0    0      x
0 0    271     0        1     0      0   0     0    0      x
0 0    271     0        1     0      0   1     0    0      x
0 0    565     0        1     0      0   0     0    0      x
0 0    565     0        1     0      0   1     0    0      x
0 0   8192     0        1     0      0   0     0    0      x
0 0   8192     0        1     0      0   1     0    0      x
0 0   4355     0        1     0      0   0     0    0      x
0 0   4355     0        1     0      0   1     0    0      x
0 0  16128     0        1     0      0   0     0    0      x
0 0  16128     0        1     0      0   1     0    0      x
0 0      0     0        0     1      0   0     0    0      x
0 0      0     0        0     1      0   1     0    0      x
0 0      0     0        0     0      0   0     x    0      x
0 0      0     0        0     0      0   1     x    0      x
0 0      0     0        0     0      0   0     x    0      x
0 0      0     0        0     0      0   1     x    0      x
0 0      0     0        0     0      0   0     x    0      x
0 0      0     0        0     0      0   1     x    0      x
0 0      0     0        0     0      0   0     x    0      x
0 0      0     0        0     0      0   1     x    0      x
0 0      0     0        0     0      0   0     x    0      x
0 0      0     0        0     0      0   1     x    0      x
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*/

/* Test case 02_P01T02:
M N progIn reset progLoad start result clk valid done output
0 0      0     0        0     0      0   0     x    x      x
0 0      0     0        0     0      0   1     x    x      x
0 0      0     1        0     0      0   0     x    x      x
0 0      0     1        0     0      0   1     0    0      x
0 0      0     0        0     0      0   0     0    0      x
0 0      0     0        0     0      0   1     0    0      x
0 0      0     0        0     0      0   0     0    0      x
0 0      0     0        0     0      0   1     0    0      x
0 0      0     0        0     0      0   0     0    0      x
0 0      0     0        0     0      0   1     0    0      x
0 0      0     0        0     0      0   0     0    0      x
0 0      0     0        0     0      0   1     0    0      x
0 0      0     0        0     0      0   0     0    0      x
0 0      0     0        0     0      0   1     0    0      x
0 0      0     0        0     0      0   0     0    0      x
0 0      0     0        0     0      0   1     0    0      x
0 0      0     0        0     0      0   0     0    0      x
0 0      0     0        0     0      0   1     0    0      x
0 0      0     0        0     0      0   0     0    0      x
0 0      0     0        0     0      0   1     0    0      x
0 0      0     0        0     0      0   0     0    0      x
0 0      0     0        0     0      0   1     0    0      x
0 0      0     0        0     0      0   0     0    0      x
0 0      0     0        0     0      0   1     0    0      x
0 0      0     0        0     0      0   0     0    0      x
0 0      0     0        0     0      0   1     0    0      x
0 0      0     0        0     0      0   0     0    0      x
0 0      0     0        0     0      0   1     0    0      x
0 0      0     0        0     0      0   0     0    0      x
0 0      0     0        0     0      0   1     0    0      x
0 0      0     0        0     0      0   0     0    0      x
0 0      0     0        0     0      0   1     0    0      x
0 0      0     0        0     0      0   0     0    0      x
0 0      0     0        0     0      0   1     0    0      x
0 0      0     0        0     0      0   0     0    0      x
0 0      0     0        0     0      0   1     0    0      x
0 0      0     0        0     0      0   0     0    0      x
0 0      0     0        0     0      0   1     0    0      x
0 0      0     0        0     0      0   0     0    0      x
0 0      0     0        0     0      0   1     0    0      x
0 0      0     0        0     0      0   0     0    0      x
0 0      0     0        0     0      0   1     0    0      x
0 0    271     0        1     0      0   0     0    0      x
0 0    271     0        1     0      0   1     0    0      x
0 0    565     0        1     0      0   0     0    0      x
0 0    565     0        1     0      0   1     0    0      x
0 0   8192     0        1     0      0   0     0    0      x
0 0   8192     0        1     0      0   1     0    0      x
0 0   4355     0        1     0      0   0     0    0      x
0 0   4355     0        1     0      0   1     0    0      x
0 0  16128     0        1     0      0   0     0    0      x
0 0  16128     0        1     0      0   1     0    0      x
0 0      0     0        0     1      0   0     0    0      x
0 0      0     0        0     1      0   1     0    0      x
0 0      0     0        0     0      0   0     x    0      x
0 0      0     0        0     0      0   1     x    0      x
0 0      0     0        0     0      0   0     x    0      x
0 0      0     0        0     0      0   1     x    0      x
0 0      0     0        0     0      0   0     x    0      x
0 0      0     0        0     0      0   1     x    0      x
0 0      0     0        0     0      0   0     x    0      x
0 0      0     0        0     0      0   1     x    0      x
0 0      0     0        0     0      0   0     x    0      x
0 0      0     0        0     0      0   1     x    0      x
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*/

/* Test case 03_P02T01:
M N progIn reset progLoad start result clk valid done output
0 0      0     0        0     0      0   0     x    x      x
0 0      0     0        0     0      0   1     x    x      x
0 0      0     1        0     0      0   0     x    x      x
0 0      0     1        0     0      0   1     0    0      x
0 0      0     0        0     0      0   0     0    0      x
0 0      0     0        0     0      0   1     0    0      x
0 0      0     0        0     0      0   0     0    0      x
0 0      0     0        0     0      0   1     0    0      x
0 0      0     0        0     0      0   0     0    0      x
0 0      0     0        0     0      0   1     0    0      x
0 0      0     0        0     0      0   0     0    0      x
0 0      0     0        0     0      0   1     0    0      x
0 0      0     0        0     0      0   0     0    0      x
0 0      0     0        0     0      0   1     0    0      x
0 0      0     0        0     0      0   0     0    0      x
0 0      0     0        0     0      0   1     0    0      x
0 0      0     0        0     0      0   0     0    0      x
0 0      0     0        0     0      0   1     0    0      x
0 0      0     0        0     0      0   0     0    0      x
0 0      0     0        0     0      0   1     0    0      x
0 0      0     0        0     0      0   0     0    0      x
0 0      0     0        0     0      0   1     0    0      x
0 0      0     0        0     0      0   0     0    0      x
0 0      0     0        0     0      0   1     0    0      x
0 0      0     0        0     0      0   0     0    0      x
0 0      0     0        0     0      0   1     0    0      x
0 0      0     0        0     0      0   0     0    0      x
0 0      0     0        0     0      0   1     0    0      x
0 0      0     0        0     0      0   0     0    0      x
0 0      0     0        0     0      0   1     0    0      x
0 0      0     0        0     0      0   0     0    0      x
0 0      0     0        0     0      0   1     0    0      x
0 0      0     0        0     0      0   0     0    0      x
0 0      0     0        0     0      0   1     0    0      x
0 0      0     0        0     0      0   0     0    0      x
0 0      0     0        0     0      0   1     0    0      x
0 0      0     0        0     0      0   0     0    0      x
0 0      0     0        0     0      0   1     0    0      x
0 0      0     0        0     0      0   0     0    0      x
0 0      0     0        0     0      0   1     0    0      x
0 0      0     0        0     0      0   0     0    0      x
0 0      0     0        0     0      0   1     0    0      x
0 0    271     0        1     0      0   0     0    0      x
0 0    271     0        1     0      0   1     0    0      x
0 0    566     0        1     0      0   0     0    0      x
0 0    566     0        1     0      0   1     0    0      x
0 0  12288     0        1     0      0   0     0    0      x
0 0  12288     0        1     0      0   1     0    0      x
0 0   5135     0        1     0      0   0     0    0      x
0 0   5135     0        1     0      0   1     0    0      x
0 0   5646     0        1     0      0   0     0    0      x
0 0   5646     0        1     0      0   1     0    0      x
0 0   5392     0        1     0      0   0     0    0      x
0 0   5392     0        1     0      0   1     0    0      x
0 0  16128     0        1     0      0   0     0    0      x
0 0  16128     0        1     0      0   1     0    0      x
0 0      0     0        1     0      0   0     0    0      x
0 0      0     0        1     0      0   1     0    0      x
0 0      0     0        1     0      0   0     0    0      x
0 0      0     0        1     0      0   1     0    0      x
0 0      0     0        1     0      0   0     0    0      x
0 0      0     0        1     0      0   1     0    0      x
0 0      0     0        1     0      0   0     0    0      x
0 0      0     0        1     0      0   1     0    0      x
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*/
