// Digital circuit card13.dig as structural Verilog
module card13 (
  input  clk,
  input  Reset,
  input  Start,
  input  progLoad,
  input  result,
  input  [3:0] in_6,
  input  in_7,
  input  [3:0] in_8
);

  wire comparator_1_eq, comparator_2_eq, Datapath_Global_Clear, done, InstructionFSM_Enable,
       Output_Counter_Enable, PC_Write, pRAM_Addr_Sel, S_IDLE, valid;
  wire [3:0] MainFSM_Current_State, multiplexer_1_out, multiplexer_2_out, multiplexer_3_out,
       multiplexer_4_out, multiplexer_5_out, multiplexer_6_out, multiplexer_7_out, multiplexer_8_out;

  Multiplexer #(.Bits(4)) multiplexer_1 (.sel(progLoad), .in_0(4'b0001), .in_1(4'b0010), .out(multiplexer_1_out));
  Multiplexer #(.Bits(4)) multiplexer_2 (.sel(progLoad), .in_0(4'b0011), .in_1(4'b0010), .out(multiplexer_2_out));
  Multiplexer #(.Bits(4)) multiplexer_3 (.sel(Start), .in_0(4'b0011), .in_1(4'b0100), .out(multiplexer_3_out));
  Comparator #(.Bits(4)) comparator_1 (.a(in_8), .b(4'b1111), .eq(comparator_1_eq));  // open: gt, lt
  Multiplexer #(.Bits(4)) multiplexer_4 (.sel(result), .in_0(4'b0101), .in_1(4'b0110), .out(multiplexer_4_out));
  Comparator #(.Bits(4)) comparator_2 (.a(in_6), .b(4'b1111), .eq(comparator_2_eq));  // open: gt, lt
  Multiplexer #(.Bits(4)) multiplexer_5 (
    .sel(comparator_1_eq), .in_0(4'b0100), .in_1(4'b0101), .out(multiplexer_5_out));
  Multiplexer #(.Bits(4)) multiplexer_6 (
    .sel(comparator_2_eq), .in_0(4'b0110), .in_1(4'b0111), .out(multiplexer_6_out));
  Multiplexer #(.Bits(4), .Selector_Bits(3)) multiplexer_7 (
    .sel(MainFSM_Current_State[2:0]), .in_0(4'b0001), .in_1(multiplexer_1_out), .in_2(multiplexer_2_out),
    .in_3(multiplexer_3_out), .in_4(multiplexer_5_out), .in_5(multiplexer_4_out), .in_6(multiplexer_6_out),
    .in_7(4'b0111), .out(multiplexer_7_out));
  Multiplexer #(.Bits(4)) multiplexer_8 (
    .sel(Reset), .in_0(multiplexer_7_out), .in_1(4'b0000), .out(multiplexer_8_out));
  Register #(.Bits(4)) State_Reg (.D(multiplexer_8_out), .C(clk), .en(1'b1), .Q(MainFSM_Current_State));
  Decoder #(.Selector_Bits(4)) decoder_1 (
    .sel(MainFSM_Current_State), .out_0(S_IDLE), .out_2(PC_Write), .out_4(InstructionFSM_Enable),
    .out_5(valid), .out_6(Output_Counter_Enable), .out_7(done));  // open: out_1, out_3, out_8, out_9, out_10, out_11, out_12, out_13, out_14, out_15
  or or_1 (Datapath_Global_Clear, done, S_IDLE);
  Multiplexer multiplexer_9 (.sel(PC_Write), .in_0(in_7), .in_1(1'b0), .out(pRAM_Addr_Sel));

  // Other names for the same wires on the sheet: Inst_pRAM_Addr_Sel = in_7; InstructionFSM_State[3:0] = in_8;
  //   Output_Addr_Counter[3:0] = in_6; pRAM_DataIn_Sel = PC_Write; pRAM_Write = PC_Write; S_PROG_LOAD = PC_Write;
  //   rRAM_Addr_Sel = Output_Counter_Enable; rRAM_Read = Output_Counter_Enable
endmodule
