// Digital circuit card3and4.dig as structural Verilog
module card3and4 (
);

  wire A, add_1_s, and_1_out, B, Carry, clk, comparator_1_eq, comparator_1_gt, comparator_1_lt, EQ, GT, LT,
       or_1_out, or_2_out, or_3_out, or_4_out, reset, sub_1_c_o;
  wire [2:0] ALU_Op;
  wire [7:0] EQout, GTout, LTout, Result;

  Add add_1 (.a(A), .b(B), .c_i(Carry), .s(add_1_s));  // open: c_o
  Sub sub_1 (.a(A), .b(B), .c_i(Carry), .c_o(sub_1_c_o));  // open: s
  and and_1 (and_1_out, A, B);
  or or_1 (or_1_out, A, B);
  Comparator comparator_1 (.a(A), .b(B), .gt(comparator_1_gt), .eq(comparator_1_eq), .lt(comparator_1_lt));
  Multiplexer #(.Selector_Bits(3)) multiplexer_1 (
    .sel(ALU_Op), .in_0(add_1_s), .in_1(sub_1_c_o), .in_2(and_1_out), .in_3(or_1_out),
    .in_4(comparator_1_gt), .in_5(comparator_1_eq), .in_6(comparator_1_lt), .out(Result[0]));  // open: in_7
  or or_2 (or_2_out, reset, GT);
  or or_3 (or_3_out, reset, EQ);
  or or_4 (or_4_out, reset, LT);
  Register #(.Bits(8)) u_GT (.D(Result), .C(clk), .en(or_2_out), .Q(GTout));
  Register #(.Bits(8)) u_EQ (.D(Result), .C(clk), .en(or_3_out), .Q(EQout));
  Register #(.Bits(8)) u_LT (.D(Result), .C(clk), .en(or_4_out), .Q(LTout));
  // Pins of 1 and 8 bits meet at Result
endmodule
