// Digital circuit card5.dig as structural Verilog
module card5 (
  input  clk,
  input  PC_Write,
  output [7:0] out_3
);

  wire [7:0] add_1_s;

  Register #(.Bits(8)) PC_Reg (.D(add_1_s), .C(clk), .en(PC_Write), .Q(out_3));
  Add #(.Bits(8)) add_1 (.a(out_3), .b(8'h1), .c_i(1'b0), .s(add_1_s));  // open: c_o

  // Other names for the same wires on the sheet: PCout[7:0] = out_3
endmodule
