// Digital circuit card6.dig as structural Verilog
module card6 (
  input  [13:0] IR_In,
  input  IR_Write,
  input  reset,
  input  clk,
  input  [7:0] Write_Data,
  input  [1:0] Write_Address,
  input  Reg_Write,
  input  [1:0] Read_Address,
  output [13:0] IR_Out,
  output [7:0] Read_Data
);

  wire and_1_out, and_2_out, and_3_out, and_4_out, decoder_1_out_0, decoder_1_out_1, decoder_1_out_2,
       decoder_1_out_3;
  wire [7:0] accA_q, accB_q, accC_q, accD_q;

  Decoder #(.Selector_Bits(2)) decoder_1 (
    .sel(Write_Address), .out_0(decoder_1_out_0), .out_1(decoder_1_out_1), .out_2(decoder_1_out_2),
    .out_3(decoder_1_out_3));
  and and_1 (and_1_out, Reg_Write, decoder_1_out_0);
  and and_2 (and_2_out, Reg_Write, decoder_1_out_1);
  and and_3 (and_3_out, Reg_Write, decoder_1_out_2);
  and and_4 (and_4_out, Reg_Write, decoder_1_out_3);
  Register #(.Bits(14)) IR_reg (.D(IR_In), .C(clk), .en(IR_Write), .Q(IR_Out));
  Register #(.Bits(8)) accA (.D(Write_Data), .C(clk), .en(and_1_out), .Q(accA_q));
  Register #(.Bits(8)) accB (.D(Write_Data), .C(clk), .en(and_2_out), .Q(accB_q));
  Register #(.Bits(8)) accC (.D(Write_Data), .C(clk), .en(and_3_out), .Q(accC_q));
  Register #(.Bits(8)) accD (.D(Write_Data), .C(clk), .en(and_4_out), .Q(accD_q));
  Multiplexer #(.Bits(8), .Selector_Bits(2)) multiplexer_1 (
    .sel(Read_Address), .in_0(accA_q), .in_1(accB_q), .in_2(accC_q), .in_3(accD_q), .out(Read_Data));

  // Other names for the same wires on the sheet: Operand[7:0] = IR_Out[7:0]; Opcode[5:0] = IR_Out[13:8]
endmodule
