// Digital circuit datapathleft.dig as structural Verilog
module datapathleft (
  input  [7:0] M,
  input  [7:0] N,
  input  [12:0] progIN,
  input  reset,
  input  progLoad,
  input  start,
  input  result,
  input  clk,
  output valid,
  output done,
  output [7:0] \output ,
  output [7:0] Z,
  output [1:0] out_13,
  output [12:0] out_14,
  output [4:0] Instruction,
  output [7:0] out_16,
  output [7:0] out_17,
  output [7:0] out_18,
  output [4:0] Instruction_2,
  output [7:0] Number,
  output busy,
  output [15:0] \ๅ ,
  output [4:0] Instruction_3,
  output [1:0] counter,
  output [7:0] \ๅ_2 ,
  output [7:0] \ๅ_3 
);

  wire _10111eq, _10111gt, _10111ls, _11101eq, and_2_out, and_3_out, and_4_out, and_5_out, and_6_out,
       and_9_out, and_12_out, and_14_out, busy_t, cmp, comparator_1_eq, comparator_4_gt, comparator_4_lt,
       comparator_5_eq, d_ff_1_q, decoder_1_out_2, decoder_1_out_3, eq, gcd, gcden, gt, halt, lazy, ls,
       not_1_out, not_2_out, not_4_out, not_5_out, oh, or_1_out, or_2_out, or_5_out, or_6_out, or_7_out,
       or_8_out, or_9_out, or_10_out, or_11_out, prime, Q, ready, reset_Out, result_Out, yeah;
  wire [1:0] compute, counter_2_out, gcdstore;
  wire [2:0] undriven;
  wire [7:0] _17, _18, _19, _20, _21, _22, _24, _25, _26, _27, _28, _30, add_2_s, add_3_s, cache,
       counter_1_out, counter_6_out, data, demultiplexer_1_out_2, demultiplexer_1_out_3, memory,
       multiplexer_1_out, multiplexer_2_out, multiplexer_3_out, multiplexer_4_out, multiplexer_10_out,
       multiplexer_11_out, operand, rAddress, register_3_q, register_4_q, rpRam, same, sub_2_s, sub_3_s, z_t;
  wire [12:0] dIn, pRAM_d2;
  wire [12:8] pRAM_d1;
  wire [15:0] mul_2_mul, register_5_q;

  not not_1 (not_1_out, clk);
  Add #(.Bits(8)) add_1 (.a(Number), .b(out_17), .c_i(1'b0), .s(_17));  // open: c_o
  Sub #(.Bits(8)) sub_1 (.a(Number), .b(out_17), .c_i(1'b0), .s(_18));  // open: c_o
  Mul #(.Bits(4)) mul_1 (.a(Number[3:0]), .b(out_17[3:0]), .mul(_19));
  Div #(.Bits(8)) div_1 (.a(Number), .b(out_17), .q(_20));  // open: r
  Demultiplexer #(.Selector_Bits(2), .Bits(8)) demultiplexer_1 (
    .sel(gcdstore), .in(memory), .out_2(demultiplexer_1_out_2), .out_3(demultiplexer_1_out_3));  // open: out_0, out_1
  Decoder #(.Selector_Bits(2)) decoder_1 (
    .sel(gcdstore), .out_2(decoder_1_out_2), .out_3(decoder_1_out_3));  // open: out_0, out_1
  and and_1 (oh, ~Instruction[0], Instruction[1], Instruction[2], Instruction[3], Instruction[4]);  // And
  Multiplexer #(.Selector_Bits(2), .Bits(8)) multiplexer_1 (
    .sel({reset, out_13[0]}), .in_0(add_2_s), .in_1(operand), .in_2({8{1'b0}}), .in_3({8{1'b0}}),
    .out(multiplexer_1_out));
  D_FF d_ff_1 (.D(oh), .C(not_1_out), .Q(d_ff_1_q));  // open: nQ
  not not_2 (not_2_out, progLoad);
  Comparator #(.Bits(2)) comparator_1 (.a(compute), .b(2'b10), .eq(comparator_1_eq));  // open: gt, lt
  and and_2 (and_2_out, ~yeah, d_ff_1_q);  // And
  Counter #(.Bits(8)) counter_1 (.en(progLoad), .C(clk), .clr(not_2_out), .out(counter_1_out));  // open: ovf
  and and_3 (and_3_out, oh, ~lazy, comparator_1_eq);  // And
  and and_4 (and_4_out, Instruction[0], ~Instruction[1], ~Instruction[2], Instruction[3], ~Instruction[4]);  // And
  Register #(.Bits(8)) register_1 (.D(demultiplexer_1_out_2), .C(clk), .en(decoder_1_out_2), .Q(\ๅ_2 ));
  Register #(.Bits(8)) register_2 (.D(demultiplexer_1_out_3), .C(clk), .en(decoder_1_out_3), .Q(\ๅ_3 ));
  and and_5 (and_5_out, ~halt, clk, Q, ~and_2_out);  // And
  Multiplexer #(.Bits(8)) multiplexer_2 (
    .sel(and_4_out), .in_0(counter_1_out), .in_1(operand), .out(multiplexer_2_out));
  D_FF #(.Bits(13)) d_ff_2 (.D(progIN), .C(~clk), .Q(dIn));  // open: nQ
  D_FF #(.Bits(8)) pc (.D(multiplexer_1_out), .C(and_5_out), .Q(Z));  // open: nQ
  and and_6 (and_6_out, ~comparator_5_eq, oh);  // And
  Div #(.Bits(8)) div_2 (.a(Number), .b(out_17), .r(_21));  // open: q
  Comparator #(.Bits(8)) comparator_2 (.a(Number), .b(out_17), .gt(_10111gt), .eq(_10111eq), .lt(_10111ls));
  assign _24 = ~Number;  // Not not_3, 8 bits wide
  Multiplexer #(.Bits(8)) multiplexer_3 (.sel(gcd), .in_0(sub_2_s), .in_1(\ๅ_2 ), .out(multiplexer_3_out));
  Multiplexer #(.Bits(8)) multiplexer_4 (.sel(gcd), .in_0(sub_3_s), .in_1(\ๅ_3 ), .out(multiplexer_4_out));
  Counter #(.Bits(2)) counter_2 (.en(and_3_out), .C(clk), .clr(yeah), .out(counter_2_out));  // open: ovf
  not not_4 (not_4_out, clk);
  not not_5 (not_5_out, clk);
  Multiplexer #(.Bits(8)) multiplexer_5 (.sel(and_2_out), .in_0(Z), .in_1(same), .out(same));
  Register #(.Bits(8)) register_3 (.D(multiplexer_3_out), .C(clk), .en(or_1_out), .Q(register_3_q));
  Register #(.Bits(8)) register_4 (.D(multiplexer_4_out), .C(clk), .en(or_2_out), .Q(register_4_q));
  Comparator #(.Bits(2)) comparator_3 (.a(counter_2_out), .b(2'b00), .gt(lazy));  // open: eq, lt
  Register #(.Bits(8)) u_cache (.D(data), .C(not_4_out), .en(1'b1), .Q(cache));
  Register #(.Bits(3)) write_remem (.D(undriven), .C(not_5_out), .en(1'b1));  // open: Q
  Add #(.Bits(8)) add_2 (.a(Z), .b(8'h1), .c_i(1'b0), .s(add_2_s));  // open: c_o
  RAMDualAccess #(.AddrBits(8), .Bits(13)) pRAM (
    .str(progLoad), .C(clk), .ld(and_4_out), .A1(multiplexer_2_out), .Din1(dIn), .A2(same),
    .D1({pRAM_d1, rpRam}), .D2(pRAM_d2));
  Add #(.Bits(8)) add_3 (.a(8'he), .b({{6{1'b0}}, counter}), .c_i(1'b0), .s(add_3_s));  // open: c_o
  Counter #(.Bits(2)) counter_3 (.en(and_6_out), .C(clk), .clr(yeah), .out(compute));  // open: ovf
  ROM #(.AddrBits(6), .Bits(8)) rom_1 (.A({out_17[2:0], Number[2:0]}), .sel(1'b1), .D(_22));
  Comparator #(.Bits(8)) comparator_4 (
    .a(register_3_q), .b(register_4_q), .gt(comparator_4_gt), .eq(busy_t), .lt(comparator_4_lt));
  or or_1 (or_1_out, gcd, comparator_4_gt);
  RAMDualAccess ramdualaccess_1 (
    .str(1'b1), .C(clk), .ld(1'b1), .A1(2'b00), .Din1(1'b1), .A2(counter_2_out), .D2(gcd));  // open: D1
  Comparator #(.Bits(2)) comparator_5 (.a(compute), .b(2'b10), .eq(comparator_5_eq));  // open: gt, lt
  or or_2 (or_2_out, gcd, comparator_4_lt);
  Multiplexer #(.Bits(13)) multiplexer_6 (
    .sel(reset), .in_0(pRAM_d2), .in_1({13{1'b0}}), .out({Instruction, out_14[7:0]}));
  assign z_t = busy_t ? register_4_q : 8'bz;  // Driver driver_1
  or or_3 (gcdstore[0], gcden, compute[0]);
  and and_7 (gcdstore[1], oh, ~comparator_5_eq);  // And
  assign _26 = Number | out_17;  // Or or_4, 8 bits wide
  Sub #(.Bits(8)) sub_2 (.a(register_3_q), .b(register_4_q), .c_i(1'b0), .s(sub_2_s));  // open: c_o
  Sub #(.Bits(8)) sub_3 (.a(register_4_q), .b(register_3_q), .c_i(1'b0), .s(sub_3_s));  // open: c_o
  Multiplexer #(.Selector_Bits(2), .Bits(8)) multiplexer_7 (
    .sel(gcdstore), .in_0(out_14[7:0]), .in_1(add_3_s), .in_2({4'b0000, out_14[3:0]}),
    .in_3({4'b0000, out_14[7:4]}), .out(operand));
  assign _25 = Number & out_17;  // And and_8, 8 bits wide
  assign _27 = Number ^ out_17;  // XOr xor_1, 8 bits wide
  BarrelShifter #(.Bits(8)) barrelshifter_1 (.in(Number), .shift({1'b0, out_17[2:0]}), .out(_28));
  Mul #(.Bits(8)) mul_2 (.a(\ๅ_2 ), .b(\ๅ_3 ), .mul(mul_2_mul));
  and and_9 (and_9_out, oh, ~yeah, gcd);  // And
  Seven_Seg_Hex seven_seg_hex_1 (.d(z_t[7:4]), .dp(1'b0));
  buf or_5 (or_5_out, reset);  // Or open: In_2
  buf or_6 (or_6_out, reset);  // Or open: In_2
  buf or_7 (or_7_out, reset);  // Or open: In_2
  Multiplexer #(.Selector_Bits(5), .Bits(8)) multiplexer_8 (
    .in_0({8{1'b0}}), .in_1(operand), .in_2(operand), .in_3(out_17), .in_4(Number), .in_5(Number),
    .in_6(out_16), .in_7(M), .in_8(N), .in_9(rpRam), .in_10(memory), .in_11(Number), .in_12(operand),
    .in_13(operand), .in_14(operand), .in_15(operand), .in_16(operand), .in_17(_17), .in_18(_18),
    .in_19(_19), .in_20(_20), .in_21(_21), .in_22(_22), .in_23(8'h5), .in_24(_24), .in_25(_25), .in_26(_26),
    .in_27(_27), .in_28(_28), .in_29(8'h5), .in_30(_30), .in_31({8{1'b0}}), .out(data));  // open: sel
  and and_10 (cmp, Instruction[0], Instruction[1], Instruction[2], ~Instruction[3], Instruction[4]);  // And
  and and_11 (prime, Instruction[0], ~Instruction[1], Instruction[2], Instruction[3], Instruction[4]);  // And
  Register #(.Bits(16)) register_5 (.D(mul_2_mul), .C(clk), .en(and_9_out), .Q(register_5_q));
  Seven_Seg_Hex seven_seg_hex_2 (.d(z_t[3:0]), .dp(1'b0));
  Register #(.Bits(8)) accA (.D(data), .C(clk), .en(or_5_out), .Q(Number));
  Register #(.Bits(8)) accB (.D(data), .C(clk), .en(or_6_out), .Q(out_17));
  Register #(.Bits(8)) regC (.D(data), .C(clk), .en(or_7_out), .Q(out_16));
  ROM #(.AddrBits(8)) rom_2 (.A(Number), .sel(1'b1), .D(_11101eq));
  and and_12 (and_12_out, _10111eq, cmp);
  not not_6 (busy, busy_t);
  or or_8 (or_8_out, _11101eq, and_12_out);
  or or_9 (or_9_out, prime, cmp);
  Div #(.Bits(16)) div_3 (.a(register_5_q), .b({{8{1'b0}}, z_t}), .q(\ๅ ));  // open: r
  and and_13 (gcden, ~busy, ~yeah, oh, lazy);  // And
  Register equal_flag (.D(or_8_out), .C(clk), .en(or_9_out), .Q(eq));
  Register greater_flag (.D(_10111gt), .C(clk), .en(cmp), .Q(gt));
  Register lesser_flag (.D(_10111ls), .C(clk), .en(cmp), .Q(ls));
  Counter #(.Bits(2)) counter_4 (.en(gcden), .C(clk), .clr(gcd), .out(counter));  // open: ovf
  Counter #(.Bits(8)) counter_5 (.en(reset_Out), .C(clk), .clr(ready), .out(rAddress));  // open: ovf
  and and_14 (and_14_out, result_Out, ~done, halt);  // And
  or or_10 (or_10_out, start, reset, result, progLoad);
  Multiplexer #(.Selector_Bits(2), .Bits(8)) multiplexer_9 (
    .sel(counter), .in_0(\ๅ [15:8]), .in_1(\ๅ [7:0]), .in_2({8{1'b0}}), .in_3({8{1'b0}}), .out(_30));
  Counter #(.Bits(8)) counter_6 (
    .en(and_14_out), .C(clk), .clr(or_10_out), .out({counter_6_out[7:5], done, counter_6_out[3:0]}));  // open: ovf
  Comparator #(.Bits(2)) comparator_6 (.a(counter), .b(2'b10), .eq(yeah));  // open: gt, lt
  Comparator #(.Bits(8)) comparator_7 (.a(rAddress), .b(8'h10), .eq(ready));  // open: gt, lt
  Multiplexer #(.Bits(8)) multiplexer_10 (.sel(reset_Out), .in_0(operand), .in_1(rAddress), .out(multiplexer_10_out));
  or or_11 (or_11_out, gcden, reset_Out);  // open: In_1
  Multiplexer #(.Bits(8)) multiplexer_11 (.sel(reset_Out), .in_0(data), .in_1({8{1'b0}}), .out(multiplexer_11_out));
  RAMDualAccess #(.AddrBits(8), .Bits(8)) rRAM (
    .str(or_11_out), .C(clk), .ld(1'b1), .A1(multiplexer_10_out), .Din1(multiplexer_11_out),
    .A2({counter_6_out[7:5], done, counter_6_out[3:0]}), .D1(memory), .D2(\output ));
  Seven_Seg_Hex seven_seg_hex_3 (.d(\output [7:4]), .dp(1'b0));
  Seven_Seg_Hex seven_seg_hex_4 (.d(\output [3:0]), .dp(1'b0));

  assign Instruction_2 = Instruction;
  assign Instruction_3 = Instruction;
  assign out_13[1] = reset;
  assign out_14[12:8] = Instruction;
  assign out_18 = Number;

  // Other names for the same wires on the sheet: st = done; a[7:0] = \ๅ_2 ; accAout[7:0] = Number;
  //   accBout[7:0] = out_17; b[7:0] = \ๅ_3 ; jump = out_13[0]; opCode[4:0] = Instruction; pc[7:0] = Z;
  //   pIn[12:0] = progIN; pLoad = progLoad; regCout[7:0] = out_16; result_In = result; whaaat[1:0] = counter

  // Notes on the sheet:
  //   test case
  //   Input
  //   Control Unit
  //   10001
  //   10010
  //   10011
  //   10100
  //   11110
  //   Jump
  //   10110
  //   10101
  //   10111
  //   11000
  //   Cache
  //   a
  //   b
  //   contents of rom_1 (hex, n*v repeats v):
  //   0,7*1,0,1,2,3,4,5,6,7,0,1,4,9,10,19,24,31,0,1,8,1b,40,7d,d8,157
  //   ,0,1,10,51,100,41,510,961,0,1,20,f3,400,c35,1e60,41a7,0,1,40,2d9
  //   ,1000,3d09,b640,44f1,0,1,80,88b,4000,1312d,44580,c90f7
  //   11001
  //   11010
  //   11011
  //   11100
  //   Register
  //   Alu
  //   flag
  //   11101
  //   contents of rom_2 (hex, n*v repeats v):
  //   0,0,1,1,0,1,0,1,0,0,0,1,0,1,0,0,0,1,0,1,0,0,0,1,5*0,1,0,1,5*0
  //   ,1,0,0,0,1,0,1,0,0,0,1,5*0,1,5*0,1,0,1,5*0,1,0,0,0,1,0,1,5*0,1
  //   ,0,0,0,1,5*0,1,7*0,1,0,0,0,1,0,1,0,0,0,1,0,1,0,0,0,1,13*0,1,0,0,0
  //   ,1,5*0,1,0,1,9*0,1,0,1,5*0,1,5*0,1,0,0,0,1,5*0,1,5*0,1,0,1,9*0
  //   ,1,0,1,0,0,0,1,0,1,11*0,1,11*0,1,0,0,0,1,0,1,0,0,0,1,5*0,1,0,1
  //   ,9*0,1
  //   Memory
endmodule

/* Test case test1:
M N progIN reset progLoad start result clk valid done output
0 0 0 0 0 0 0 0 x x x
0 0 0 0 0 0 0 1 x x x
0 0 0 1 0 0 0 0 x x x
0 0 0 1 0 0 0 1 0 0 0
0 0 0 0 0 0 0 0 0 0 0
0 0 0 0 0 0 0 1 0 0 0
0 0 0 0 0 0 0 0 0 0 0
0 0 0 0 0 0 0 1 0 0 0
0 0 0 0 0 0 0 0 0 0 0
0 0 0 0 0 0 0 1 0 0 0
0 0 0 0 0 0 0 0 0 0 0
0 0 0 0 0 0 0 1 0 0 0
0 0 0 0 0 0 0 0 0 0 0
0 0 0 0 0 0 0 1 0 0 0
0 0 0 0 0 0 0 0 0 0 0
0 0 0 0 0 0 0 1 0 0 0
0 0 0 0 0 0 0 0 0 0 0
0 0 0 0 0 0 0 1 0 0 0
0 0 0 0 0 0 0 0 0 0 0
0 0 0 0 0 0 0 1 0 0 0
0 0 0 0 0 0 0 0 0 0 0
0 0 0 0 0 0 0 1 0 0 0
0 0 0 0 0 0 0 0 0 0 0
0 0 0 0 0 0 0 1 0 0 0
0 0 0 0 0 0 0 0 0 0 0
0 0 0 0 0 0 0 1 0 0 0
0 0 0 0 0 0 0 0 0 0 0
0 0 0 0 0 0 0 1 0 0 0
0 0 0 0 0 0 0 0 0 0 0
0 0 0 0 0 0 0 1 0 0 0
0 0 0 0 0 0 0 0 0 0 0
0 0 0 0 0 0 0 1 0 0 0
0 0 0 0 0 0 0 0 0 0 0
0 0 0 0 0 0 0 1 0 0 0
0 0 0 0 0 0 0 0 0 0 0
0 0 0 0 0 0 0 1 0 0 0
0 0 0 0 0 0 0 0 0 0 0
0 0 0 0 0 0 0 1 0 0 0
0 0 0 0 0 0 0 0 0 0 0
0 0 0 0 0 0 0 1 0 0 0
0 0 0 0 0 0 0 0 0 0 0
0 0 0 0 0 0 0 1 0 0 0
0 0 271 0 1 0 0 0 0 0 0
0 0 271 0 1 0 0 1 0 0 0
0 0 566 0 1 0 0 0 0 0 0
0 0 566 0 1 0 0 1 0 0 0
0 0 5888 0 1 0 0 0 0 0 0
0 0 5888 0 1 0 0 1 0 0 0
0 0 3599 0 1 0 0 0 0 0 0
0 0 3599 0 1 0 0 1 0 0 0
0 0 4110 0 1 0 0 0 0 0 0
0 0 4110 0 1 0 0 1 0 0 0
0 0 3856 0 1 0 0 0 0 0 0
0 0 3856 0 1 0 0 1 0 0 0
0 0 0 0 1 0 0 0 0 0 0
0 0 0 0 1 0 0 1 0 0 0
0 0 0 0 1 0 0 0 0 0 0
0 0 0 0 1 0 0 1 0 0 0
0 0 0 0 1 0 0 0 0 0 0
0 0 0 0 1 0 0 1 0 0 0
0 0 0 0 1 0 0 0 0 0 0
0 0 0 0 1 0 0 1 0 0 0
0 0 0 0 1 0 0 0 0 0 0
0 0 0 0 1 0 0 1 0 0 0
0 0 0 0 1 0 0 0 0 0 0
0 0 0 0 1 0 0 1 0 0 0
0 0 0 0 1 0 0 0 0 0 0
0 0 0 0 1 0 0 1 0 0 0
0 0 0 0 1 0 0 0 0 0 0
0 0 0 0 1 0 0 1 0 0 0
0 0 0 0 1 0 0 0 0 0 0
0 0 0 0 1 0 0 1 0 0 0
0 0 0 0 1 0 0 0 0 0 0
0 0 0 0 1 0 0 1 0 0 0
0 0 4352 0 1 0 0 0 0 0 0
0 0 4352 0 1 0 0 1 0 0 0
0 0 2819 0 1 0 0 0 0 0 0
0 0 2819 0 1 0 0 1 0 0 0
0 0 7936 0 1 0 0 0 0 0 0
0 0 7936 0 1 0 0 1 0 0 0
0 0 0 0 1 0 0 0 0 0 0
0 0 0 0 1 0 0 1 0 0 0
0 0 0 0 0 0 0 0 0 0 0
0 0 0 0 0 0 0 1 0 0 0
0 0 0 0 0 0 0 0 0 0 0
0 0 0 0 0 0 0 1 0 0 0
0 0 0 0 0 0 0 0 0 0 0
0 0 0 0 0 0 0 1 0 0 0
0 0 0 0 0 1 0 0 0 0 0
0 0 0 0 0 1 0 1 0 0 0
0 0 0 0 0 0 0 0 x 0 0
0 0 0 0 0 0 0 1 x 0 0
0 0 0 0 0 0 0 0 x 0 0
0 0 0 0 0 0 0 1 x 0 0
0 0 0 0 0 0 0 0 x 0 0
0 0 0 0 0 0 0 1 x 0 0
0 0 0 0 0 0 0 0 x 0 0
0 0 0 0 0 0 0 1 x 0 0
0 0 0 0 0 0 0 0 x 0 0
0 0 0 0 0 0 0 1 x 0 0
0 0 0 0 0 0 0 0 x 0 0
0 0 0 0 0 0 0 1 x 0 0
0 0 0 0 0 0 0 0 x 0 0
0 0 0 0 0 0 0 1 x 0 0
0 0 0 0 0 0 0 0 x 0 0
0 0 0 0 0 0 0 1 x 0 0
0 0 0 0 0 0 0 0 x 0 0
0 0 0 0 0 0 0 1 x 0 0
0 0 0 0 0 0 0 0 x 0 0
0 0 0 0 0 0 0 1 x 0 0
0 0 0 0 0 0 0 0 x 0 0
0 0 0 0 0 0 0 1 x 0 0
0 0 0 0 0 0 0 0 x 0 0
0 0 0 0 0 0 0 1 x 0 0
0 0 0 0 0 0 0 0 x 0 0
0 0 0 0 0 0 0 1 x 0 0
0 0 0 0 0 0 0 0 x 0 0
0 0 0 0 0 0 0 1 x 0 0
0 0 0 0 0 0 0 0 x 0 0
0 0 0 0 0 0 0 1 x 0 0
0 0 0 0 0 0 0 0 x 0 0
0 0 0 0 0 0 0 1 x 0 0
0 0 0 0 0 0 0 0 x 0 0
0 0 0 0 0 0 0 1 x 0 0
0 0 0 0 0 0 0 0 x 0 0
0 0 0 0 0 0 0 1 x 0 0
0 0 0 0 0 0 0 0 x 0 0
0 0 0 0 0 0 0 1 x 0 0
0 0 0 0 0 0 0 0 x 0 0
0 0 0 0 0 0 0 1 x 0 0
0 0 0 0 0 0 0 0 x 0 0
0 0 0 0 0 0 0 1 x 0 0
0 0 0 0 0 0 0 0 x 0 0
0 0 0 0 0 0 0 1 x 0 0
0 0 0 0 0 0 0 0 x 0 0
0 0 0 0 0 0 0 1 x 0 0
0 0 0 0 0 0 0 0 x 0 0
0 0 0 0 0 0 0 1 x 0 0
0 0 0 0 0 0 0 0 x 0 0
0 0 0 0 0 0 0 1 x 0 0
0 0 0 0 0 0 0 0 x 0 0
0 0 0 0 0 0 0 1 1 0 0
0 0 0 0 0 0 1 0 1 0 0
0 0 0 0 0 0 1 1 1 0 0
0 0 0 0 0 0 0 0 1 0 0
0 0 0 0 0 0 0 1 1 0 0
0 0 0 0 0 0 0 0 1 0 0
0 0 0 0 0 0 0 1 1 0 0
0 0 0 0 0 0 0 0 1 0 0
0 0 0 0 0 0 0 1 1 0 69
0 0 0 0 0 0 0 0 1 0 69
0 0 0 0 0 0 0 1 1 0 0
0 0 0 0 0 0 0 0 1 0 0
0 0 0 0 0 0 0 1 1 0 0
0 0 0 0 0 0 0 0 1 0 0
0 0 0 0 0 0 0 1 1 0 0
0 0 0 0 0 0 0 0 1 0 0
0 0 0 0 0 0 0 1 1 0 0
0 0 0 0 0 0 0 0 1 0 0
0 0 0 0 0 0 0 1 1 0 0
0 0 0 0 0 0 0 0 1 0 0
0 0 0 0 0 0 0 1 1 0 0
0 0 0 0 0 0 0 0 1 0 0
0 0 0 0 0 0 0 1 1 0 0
0 0 0 0 0 0 0 0 1 0 0
0 0 0 0 0 0 0 1 1 0 0
0 0 0 0 0 0 0 0 1 0 0
0 0 0 0 0 0 0 1 1 0 0
0 0 0 0 0 0 0 0 1 0 0
0 0 0 0 0 0 0 1 1 0 0
0 0 0 0 0 0 0 0 1 0 0
0 0 0 0 0 0 0 1 1 0 0
0 0 0 0 0 0 0 0 1 0 0
0 0 0 0 0 0 0 1 1 0 0
0 0 0 0 0 0 0 0 1 0 0
0 0 0 0 0 0 0 1 1 1 0
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*/

/* Test case test2:
M N progIN reset progLoad start result clk valid done output
0 0 0 0 0 0 0 0 x x x
0 0 0 0 0 0 0 1 x x x
0 0 0 1 0 0 0 0 x x x
0 0 0 1 0 0 0 1 0 0 x
0 0 0 0 0 0 0 0 0 0 x
0 0 0 0 0 0 0 1 0 0 x
0 0 0 0 0 0 0 0 0 0 x
0 0 0 0 0 0 0 1 0 0 x
0 0 0 0 0 0 0 0 0 0 x
0 0 0 0 0 0 0 1 0 0 x
0 0 0 0 0 0 0 0 0 0 x
0 0 0 0 0 0 0 1 0 0 x
0 0 0 0 0 0 0 0 0 0 x
0 0 0 0 0 0 0 1 0 0 x
0 0 0 0 0 0 0 0 0 0 x
0 0 0 0 0 0 0 1 0 0 x
0 0 0 0 0 0 0 0 0 0 x
0 0 0 0 0 0 0 1 0 0 x
0 0 0 0 0 0 0 0 0 0 x
0 0 0 0 0 0 0 1 0 0 x
0 0 0 0 0 0 0 0 0 0 x
0 0 0 0 0 0 0 1 0 0 x
0 0 0 0 0 0 0 0 0 0 x
0 0 0 0 0 0 0 1 0 0 x
0 0 0 0 0 0 0 0 0 0 x
0 0 0 0 0 0 0 1 0 0 x
0 0 0 0 0 0 0 0 0 0 x
0 0 0 0 0 0 0 1 0 0 x
0 0 0 0 0 0 0 0 0 0 x
0 0 0 0 0 0 0 1 0 0 x
0 0 0 0 0 0 0 0 0 0 x
0 0 0 0 0 0 0 1 0 0 x
0 0 0 0 0 0 0 0 0 0 x
0 0 0 0 0 0 0 1 0 0 x
0 0 0 0 0 0 0 0 0 0 x
0 0 0 0 0 0 0 1 0 0 x
0 0 0 0 0 0 0 0 0 0 x
0 0 0 0 0 0 0 1 0 0 x
0 0 0 0 0 0 0 0 0 0 x
0 0 0 0 0 0 0 1 0 0 x
0 0 0 0 0 0 0 0 0 0 x
0 0 0 0 0 0 0 1 0 0 x
0 0 271 0 1 0 0 0 0 0 x
0 0 271 0 1 0 0 1 0 0 x
0 0 565 0 1 0 0 0 0 0 x
0 0 565 0 1 0 0 1 0 0 x
0 0 4352 0 1 0 0 0 0 0 x
0 0 4352 0 1 0 0 1 0 0 x
0 0 2819 0 1 0 0 0 0 0 x
0 0 2819 0 1 0 0 1 0 0 x
0 0 7936 0 1 0 0 0 0 0 x
0 0 7936 0 1 0 0 1 0 0 x
0 0 0 0 0 1 0 0 0 0 x
0 0 0 0 0 1 0 1 0 0 x
0 0 0 0 0 0 0 0 x 0 x
0 0 0 0 0 0 0 1 x 0 x
0 0 0 0 0 0 0 0 x 0 x
0 0 0 0 0 0 0 1 x 0 x
0 0 0 0 0 0 0 0 x 0 x
0 0 0 0 0 0 0 1 x 0 x
0 0 0 0 0 0 0 0 x 0 x
0 0 0 0 0 0 0 1 x 0 x
0 0 0 0 0 0 0 0 x 0 x
0 0 0 0 0 0 0 1 x 0 x
0 0 0 0 0 0 0 0 x 0 x
0 0 0 0 0 0 0 1 x 0 x
0 0 0 0 0 0 0 0 x 0 x
0 0 0 0 0 0 0 1 x 0 x
0 0 0 0 0 0 0 0 x 0 x
0 0 0 0 0 0 0 1 x 0 x
0 0 0 0 0 0 0 0 x 0 x
0 0 0 0 0 0 0 1 x 0 x
0 0 0 0 0 0 0 0 x 0 x
0 0 0 0 0 0 0 1 x 0 x
0 0 0 0 0 0 0 0 x 0 x
0 0 0 0 0 0 0 1 x 0 x
0 0 0 0 0 0 0 0 x 0 x
0 0 0 0 0 0 0 1 x 0 x
0 0 0 0 0 0 0 0 x 0 x
0 0 0 0 0 0 0 1 x 0 x
0 0 0 0 0 0 0 0 x 0 x
0 0 0 0 0 0 0 1 x 0 x
0 0 0 0 0 0 0 0 x 0 x
0 0 0 0 0 0 0 1 x 0 x
0 0 0 0 0 0 0 0 x 0 x
0 0 0 0 0 0 0 1 x 0 x
0 0 0 0 0 0 0 0 x 0 x
0 0 0 0 0 0 0 1 x 0 x
0 0 0 0 0 0 0 0 x 0 x
0 0 0 0 0 0 0 1 x 0 x
0 0 0 0 0 0 0 0 x 0 x
0 0 0 0 0 0 0 1 x 0 x
0 0 0 0 0 0 0 0 x 0 x
0 0 0 0 0 0 0 1 x 0 x
0 0 0 0 0 0 0 0 x 0 x
0 0 0 0 0 0 0 1 x 0 x
0 0 0 0 0 0 0 0 x 0 x
0 0 0 0 0 0 0 1 x 0 x
0 0 0 0 0 0 0 0 x 0 x
0 0 0 0 0 0 0 1 x 0 x
0 0 0 0 0 0 0 0 x 0 x
0 0 0 0 0 0 0 1 x 0 x
0 0 0 0 0 0 0 0 x 0 x
0 0 0 0 0 0 0 1 x 0 x
0 0 0 0 0 0 0 0 x 0 x
0 0 0 0 0 0 0 1 1 0 x
0 0 0 0 0 0 1 0 1 0 x
0 0 0 0 0 0 1 1 1 0 0
0 0 0 0 0 0 0 0 1 0 0
0 0 0 0 0 0 0 1 1 0 0
0 0 0 0 0 0 0 0 1 0 0
0 0 0 0 0 0 0 1 1 0 0
0 0 0 0 0 0 0 0 1 0 0
0 0 0 0 0 0 0 1 1 0 68
0 0 0 0 0 0 0 0 1 0 68
0 0 0 0 0 0 0 1 1 0 0
0 0 0 0 0 0 0 0 1 0 0
0 0 0 0 0 0 0 1 1 0 0
0 0 0 0 0 0 0 0 1 0 0
0 0 0 0 0 0 0 1 1 0 0
0 0 0 0 0 0 0 0 1 0 0
0 0 0 0 0 0 0 1 1 0 0
0 0 0 0 0 0 0 0 1 0 0
0 0 0 0 0 0 0 1 1 0 0
0 0 0 0 0 0 0 0 1 0 0
0 0 0 0 0 0 0 1 1 0 0
0 0 0 0 0 0 0 0 1 0 0
0 0 0 0 0 0 0 1 1 0 0
0 0 0 0 0 0 0 0 1 0 0
0 0 0 0 0 0 0 1 1 0 0
0 0 0 0 0 0 0 0 1 0 0
0 0 0 0 0 0 0 1 1 0 0
0 0 0 0 0 0 0 0 1 0 0
0 0 0 0 0 0 0 1 1 0 0
0 0 0 0 0 0 0 0 1 0 0
0 0 0 0 0 0 0 1 1 0 0
0 0 0 0 0 0 0 0 1 0 0
0 0 0 0 0 0 0 1 1 0 0
0 0 0 0 0 0 0 0 1 0 0
0 0 0 0 0 0 0 1 1 1 x
0 0 0 0 0 0 0 0 1 1 x
0 0 0 0 0 0 0 1 1 1 x
0 0 0 0 0 0 0 0 1 1 x
*/

/* Test case test3:
M N progIN reset progLoad start result clk valid done output
0 0 0 0 0 0 0 0 x x x
0 0 0 0 0 0 0 1 x x x
0 0 0 1 0 0 0 0 x x x
0 0 0 1 0 0 0 1 0 0 x
0 0 0 0 0 0 0 0 0 0 x
0 0 0 0 0 0 0 1 0 0 x
0 0 0 0 0 0 0 0 0 0 x
0 0 0 0 0 0 0 1 0 0 x
0 0 0 0 0 0 0 0 0 0 x
0 0 0 0 0 0 0 1 0 0 x
0 0 0 0 0 0 0 0 0 0 x
0 0 0 0 0 0 0 1 0 0 x
0 0 0 0 0 0 0 0 0 0 x
0 0 0 0 0 0 0 1 0 0 x
0 0 0 0 0 0 0 0 0 0 x
0 0 0 0 0 0 0 1 0 0 x
0 0 0 0 0 0 0 0 0 0 x
0 0 0 0 0 0 0 1 0 0 x
0 0 0 0 0 0 0 0 0 0 x
0 0 0 0 0 0 0 1 0 0 x
0 0 0 0 0 0 0 0 0 0 x
0 0 0 0 0 0 0 1 0 0 x
0 0 0 0 0 0 0 0 0 0 x
0 0 0 0 0 0 0 1 0 0 x
0 0 0 0 0 0 0 0 0 0 x
0 0 0 0 0 0 0 1 0 0 x
0 0 0 0 0 0 0 0 0 0 x
0 0 0 0 0 0 0 1 0 0 x
0 0 0 0 0 0 0 0 0 0 x
0 0 0 0 0 0 0 1 0 0 x
0 0 0 0 0 0 0 0 0 0 x
0 0 0 0 0 0 0 1 0 0 x
0 0 0 0 0 0 0 0 0 0 x
0 0 0 0 0 0 0 1 0 0 x
0 0 0 0 0 0 0 0 0 0 x
0 0 0 0 0 0 0 1 0 0 x
0 0 0 0 0 0 0 0 0 0 x
0 0 0 0 0 0 0 1 0 0 x
0 0 0 0 0 0 0 0 0 0 x
0 0 0 0 0 0 0 1 0 0 x
0 0 0 0 0 0 0 0 0 0 x
0 0 0 0 0 0 0 1 0 0 x
0 0 271 0 1 0 0 0 0 0 x
0 0 271 0 1 0 0 1 0 0 x
0 0 565 0 1 0 0 0 0 0 x
0 0 565 0 1 0 0 1 0 0 x
0 0 4352 0 1 0 0 0 0 0 x
0 0 4352 0 1 0 0 1 0 0 x
0 0 2819 0 1 0 0 0 0 0 x
0 0 2819 0 1 0 0 1 0 0 x
0 0 7936 0 1 0 0 0 0 0 x
0 0 7936 0 1 0 0 1 0 0 x
0 0 0 0 0 1 0 0 0 0 x
0 0 0 0 0 1 0 1 0 0 x
0 0 0 0 0 0 0 0 x 0 x
0 0 0 0 0 0 0 1 x 0 x
0 0 0 0 0 0 0 0 x 0 x
0 0 0 0 0 0 0 1 x 0 x
0 0 0 0 0 0 0 0 x 0 x
0 0 0 0 0 0 0 1 x 0 x
0 0 0 0 0 0 0 0 x 0 x
0 0 0 0 0 0 0 1 x 0 x
0 0 0 0 0 0 0 0 x 0 x
0 0 0 0 0 0 0 1 x 0 x
0 0 0 0 0 0 0 0 x 0 x
0 0 0 0 0 0 0 1 x 0 x
0 0 0 0 0 0 0 0 x 0 x
0 0 0 0 0 0 0 1 x 0 x
0 0 0 0 0 0 0 0 x 0 x
0 0 0 0 0 0 0 1 x 0 x
0 0 0 0 0 0 0 0 x 0 x
0 0 0 0 0 0 0 1 x 0 x
0 0 0 0 0 0 0 0 x 0 x
0 0 0 0 0 0 0 1 x 0 x
0 0 0 0 0 0 0 0 x 0 x
0 0 0 0 0 0 0 1 x 0 x
0 0 0 0 0 0 0 0 x 0 x
0 0 0 0 0 0 0 1 x 0 x
0 0 0 0 0 0 0 0 x 0 x
0 0 0 0 0 0 0 1 x 0 x
0 0 0 0 0 0 0 0 x 0 x
0 0 0 0 0 0 0 1 x 0 x
0 0 0 0 0 0 0 0 x 0 x
0 0 0 0 0 0 0 1 x 0 x
0 0 0 0 0 0 0 0 x 0 x
0 0 0 0 0 0 0 1 x 0 x
0 0 0 0 0 0 0 0 x 0 x
0 0 0 0 0 0 0 1 x 0 x
0 0 0 0 0 0 0 0 x 0 x
0 0 0 0 0 0 0 1 x 0 x
0 0 0 0 0 0 0 0 x 0 x
0 0 0 0 0 0 0 1 x 0 x
0 0 0 0 0 0 0 0 x 0 x
0 0 0 0 0 0 0 1 x 0 x
0 0 0 0 0 0 0 0 x 0 x
0 0 0 0 0 0 0 1 x 0 x
0 0 0 0 0 0 0 0 x 0 x
0 0 0 0 0 0 0 1 x 0 x
0 0 0 0 0 0 0 0 x 0 x
0 0 0 0 0 0 0 1 x 0 x
0 0 0 0 0 0 0 0 x 0 x
0 0 0 0 0 0 0 1 x 0 x
0 0 0 0 0 0 0 0 x 0 x
0 0 0 0 0 0 0 1 x 0 x
0 0 0 0 0 0 0 0 x 0 x
0 0 0 0 0 0 0 1 1 0 x
0 0 0 0 0 0 1 0 1 0 x
0 0 0 0 0 0 1 1 1 0 0
0 0 0 0 0 0 0 0 1 0 0
0 0 0 0 0 0 0 1 1 0 0
0 0 0 0 0 0 0 0 1 0 0
0 0 0 0 0 0 0 1 1 0 0
0 0 0 0 0 0 0 0 1 0 0
0 0 0 0 0 0 0 1 1 0 68
0 0 0 0 0 0 0 0 1 0 68
0 0 0 0 0 0 0 1 1 0 0
0 0 0 0 0 0 0 0 1 0 0
0 0 0 0 0 0 0 1 1 0 0
0 0 0 0 0 0 0 0 1 0 0
0 0 0 0 0 0 0 1 1 0 0
0 0 0 0 0 0 0 0 1 0 0
0 0 0 0 0 0 0 1 1 0 0
0 0 0 0 0 0 0 0 1 0 0
0 0 0 0 0 0 0 1 1 0 0
0 0 0 0 0 0 0 0 1 0 0
0 0 0 0 0 0 0 1 1 0 0
0 0 0 0 0 0 0 0 1 0 0
0 0 0 0 0 0 0 1 1 0 0
0 0 0 0 0 0 0 0 1 0 0
0 0 0 0 0 0 0 1 1 0 0
0 0 0 0 0 0 0 0 1 0 0
0 0 0 0 0 0 0 1 1 0 0
0 0 0 0 0 0 0 0 1 0 0
0 0 0 0 0 0 0 1 1 0 0
0 0 0 0 0 0 0 0 1 0 0
0 0 0 0 0 0 0 1 1 0 0
0 0 0 0 0 0 0 0 1 0 0
0 0 0 0 0 0 0 1 1 0 0
0 0 0 0 0 0 0 0 1 0 0
0 0 0 0 0 0 0 1 1 1 x
0 0 0 0 0 0 0 0 1 1 x
0 0 0 0 0 0 0 1 1 1 x
0 0 0 0 0 0 0 0 1 1 x
*/

/* Test case test4:
M N progIN reset progLoad start result clk valid done output
0 0 0 0 0 0 0 0 x x x
0 0 0 0 0 0 0 1 x x x
0 0 0 1 0 0 0 0 x x x
0 0 0 1 0 0 0 1 0 0 x
0 0 0 0 0 0 0 0 0 0 x
0 0 0 0 0 0 0 1 0 0 x
0 0 0 0 0 0 0 0 0 0 x
0 0 0 0 0 0 0 1 0 0 x
0 0 0 0 0 0 0 0 0 0 x
0 0 0 0 0 0 0 1 0 0 x
0 0 0 0 0 0 0 0 0 0 x
0 0 0 0 0 0 0 1 0 0 x
0 0 0 0 0 0 0 0 0 0 x
0 0 0 0 0 0 0 1 0 0 x
0 0 0 0 0 0 0 0 0 0 x
0 0 0 0 0 0 0 1 0 0 x
0 0 0 0 0 0 0 0 0 0 x
0 0 0 0 0 0 0 1 0 0 x
0 0 0 0 0 0 0 0 0 0 x
0 0 0 0 0 0 0 1 0 0 x
0 0 0 0 0 0 0 0 0 0 x
0 0 0 0 0 0 0 1 0 0 x
0 0 0 0 0 0 0 0 0 0 x
0 0 0 0 0 0 0 1 0 0 x
0 0 0 0 0 0 0 0 0 0 x
0 0 0 0 0 0 0 1 0 0 x
0 0 0 0 0 0 0 0 0 0 x
0 0 0 0 0 0 0 1 0 0 x
0 0 0 0 0 0 0 0 0 0 x
0 0 0 0 0 0 0 1 0 0 x
0 0 0 0 0 0 0 0 0 0 x
0 0 0 0 0 0 0 1 0 0 x
0 0 0 0 0 0 0 0 0 0 x
0 0 0 0 0 0 0 1 0 0 x
0 0 0 0 0 0 0 0 0 0 x
0 0 0 0 0 0 0 1 0 0 x
0 0 0 0 0 0 0 0 0 0 x
0 0 0 0 0 0 0 1 0 0 x
0 0 0 0 0 0 0 0 0 0 x
0 0 0 0 0 0 0 1 0 0 x
0 0 0 0 0 0 0 0 0 0 x
0 0 0 0 0 0 0 1 0 0 x
0 0 406 0 1 0 0 0 0 0 x
0 0 406 0 1 0 0 1 0 0 x
0 0 761 0 1 0 0 0 0 0 x
0 0 761 0 1 0 0 1 0 0 x
0 0 2816 0 1 0 0 0 0 0 x
0 0 2816 0 1 0 0 1 0 0 x
0 0 7680 0 1 0 0 0 0 0 x
0 0 7680 0 1 0 0 1 0 0 x
0 0 7936 0 1 0 0 0 0 0 x
0 0 7936 0 1 0 0 1 0 0 x
0 0 0 0 0 1 0 0 0 0 x
0 0 0 0 0 1 0 1 0 0 x
0 0 0 0 0 0 0 0 x 0 x
0 0 0 0 0 0 0 1 x 0 x
0 0 0 0 0 0 0 0 x 0 x
0 0 0 0 0 0 0 1 x 0 x
0 0 0 0 0 0 0 0 x 0 x
0 0 0 0 0 0 0 1 x 0 x
0 0 0 0 0 0 0 0 x 0 x
0 0 0 0 0 0 0 1 x 0 x
0 0 0 0 0 0 0 0 x 0 x
0 0 0 0 0 0 0 1 x 0 x
0 0 0 0 0 0 0 0 x 0 x
0 0 0 0 0 0 0 1 x 0 x
0 0 0 0 0 0 0 0 x 0 x
0 0 0 0 0 0 0 1 x 0 x
0 0 0 0 0 0 0 0 x 0 x
0 0 0 0 0 0 0 1 x 0 x
0 0 0 0 0 0 0 0 x 0 x
0 0 0 0 0 0 0 1 x 0 x
0 0 0 0 0 0 0 0 x 0 x
0 0 0 0 0 0 0 1 x 0 x
0 0 0 0 0 0 0 0 x 0 x
0 0 0 0 0 0 0 1 x 0 x
0 0 0 0 0 0 0 0 x 0 x
0 0 0 0 0 0 0 1 x 0 x
0 0 0 0 0 0 0 0 x 0 x
0 0 0 0 0 0 0 1 x 0 x
0 0 0 0 0 0 0 0 x 0 x
0 0 0 0 0 0 0 1 x 0 x
0 0 0 0 0 0 0 0 x 0 x
0 0 0 0 0 0 0 1 x 0 x
0 0 0 0 0 0 0 0 x 0 x
0 0 0 0 0 0 0 1 x 0 x
0 0 0 0 0 0 0 0 x 0 x
0 0 0 0 0 0 0 1 x 0 x
0 0 0 0 0 0 0 0 x 0 x
0 0 0 0 0 0 0 1 x 0 x
0 0 0 0 0 0 0 0 x 0 x
0 0 0 0 0 0 0 1 x 0 x
0 0 0 0 0 0 0 0 x 0 x
0 0 0 0 0 0 0 1 x 0 x
0 0 0 0 0 0 0 0 x 0 x
0 0 0 0 0 0 0 1 x 0 x
0 0 0 0 0 0 0 0 x 0 x
0 0 0 0 0 0 0 1 x 0 x
0 0 0 0 0 0 0 0 x 0 x
0 0 0 0 0 0 0 1 x 0 x
0 0 0 0 0 0 0 0 x 0 x
0 0 0 0 0 0 0 1 x 0 x
0 0 0 0 0 0 0 0 x 0 x
0 0 0 0 0 0 0 1 x 0 x
0 0 0 0 0 0 0 0 x 0 x
0 0 0 0 0 0 0 1 1 0 x
0 0 0 0 0 0 1 0 1 0 x
0 0 0 0 0 0 1 1 1 0 0
0 0 0 0 0 0 0 0 1 0 0
0 0 0 0 0 0 0 1 1 0 0
0 0 0 0 0 0 0 0 1 0 0
0 0 0 0 0 0 0 1 1 0 0
0 0 0 0 0 0 0 0 1 0 0
0 0 0 0 0 0 0 1 1 0 0
0 0 0 0 0 0 0 0 1 0 0
0 0 0 0 0 0 0 1 1 0 0
0 0 0 0 0 0 0 0 1 0 0
0 0 0 0 0 0 0 1 1 0 0
0 0 0 0 0 0 0 0 1 0 0
0 0 0 0 0 0 0 1 1 0 0
0 0 0 0 0 0 0 0 1 0 0
0 0 0 0 0 0 0 1 1 0 0
0 0 0 0 0 0 0 0 1 0 0
0 0 0 0 0 0 0 1 1 0 0
0 0 0 0 0 0 0 0 1 0 0
0 0 0 0 0 0 0 1 1 0 0
0 0 0 0 0 0 0 0 1 0 0
0 0 0 0 0 0 0 1 1 0 0
0 0 0 0 0 0 0 0 1 0 0
0 0 0 0 0 0 0 1 1 0 0
0 0 0 0 0 0 0 0 1 0 0
0 0 0 0 0 0 0 1 1 0 0
0 0 0 0 0 0 0 0 1 0 0
0 0 0 0 0 0 0 1 1 0 0
0 0 0 0 0 0 0 0 1 0 0
0 0 0 0 0 0 0 1 1 0 0
0 0 0 0 0 0 0 0 1 0 0
0 0 0 0 0 0 0 1 1 0 0
0 0 0 0 0 0 0 0 1 0 0
0 0 0 0 0 0 0 1 1 1 x
0 0 0 0 0 0 0 0 1 1 x
0 0 0 0 0 0 0 1 1 1 x
0 0 0 0 0 0 0 0 1 1 x
*/

/* Test case 01_P01T01:
M N progIN reset progLoad start result clk valid done output
0 0 0 0 0 0 0 0 0 0 0
0 0 0 0 0 0 0 1 0 0 0
0 0 0 1 0 0 0 0 0 0 0
0 0 0 1 0 0 0 1 0 0 0
0 0 0 0 0 0 0 0 0 0 0
0 0 0 0 0 0 0 1 0 0 0
0 0 0 0 0 0 0 0 0 0 0
0 0 0 0 0 0 0 1 0 0 0
0 0 0 0 0 0 0 0 0 0 0
0 0 0 0 0 0 0 1 0 0 0
0 0 0 0 0 0 0 0 0 0 0
0 0 0 0 0 0 0 1 0 0 0
0 0 0 0 0 0 0 0 0 0 0
0 0 0 0 0 0 0 1 0 0 0
0 0 0 0 0 0 0 0 0 0 0
0 0 0 0 0 0 0 1 0 0 0
0 0 0 0 0 0 0 0 0 0 0
0 0 0 0 0 0 0 1 0 0 0
0 0 0 0 0 0 0 0 0 0 0
0 0 0 0 0 0 0 1 0 0 0
0 0 0 0 0 0 0 0 0 0 0
0 0 0 0 0 0 0 1 0 0 0
0 0 0 0 0 0 0 0 0 0 0
0 0 0 0 0 0 0 1 0 0 0
0 0 0 0 0 0 0 0 0 0 0
0 0 0 0 0 0 0 1 0 0 0
0 0 0 0 0 0 0 0 0 0 0
0 0 0 0 0 0 0 1 0 0 0
0 0 0 0 0 0 0 0 0 0 0
0 0 0 0 0 0 0 1 0 0 0
0 0 0 0 0 0 0 0 0 0 0
0 0 0 0 0 0 0 1 0 0 0
0 0 0 0 0 0 0 0 0 0 0
0 0 0 0 0 0 0 1 0 0 0
0 0 0 0 0 0 0 0 0 0 0
0 0 0 0 0 0 0 1 0 0 0
0 0 0 0 0 0 0 0 0 0 0
0 0 0 0 0 0 0 1 0 0 0
0 0 0 0 0 0 0 0 0 0 0
0 0 0 0 0 0 0 1 0 0 0
0 0 0 0 0 0 0 0 0 0 0
0 0 0 0 0 0 0 1 0 0 0
0 0 271 0 1 0 0 0 0 0 0
0 0 0 0 1 0 0 1 0 0 0
0 0 565 0 1 0 0 0 0 0 0
0 0 0 0 1 0 0 1 0 0 0
0 0 4352 0 1 0 0 0 0 0 0
0 0 0 0 1 0 0 1 0 0 0
0 0 2819 0 1 0 0 0 0 0 0
0 0 0 0 1 0 0 1 0 0 0
0 0 7936 0 1 0 0 0 0 0 0
0 0 0 0 1 0 0 1 0 0 0
0 0 0 0 0 1 0 0 0 0 0
0 0 0 0 0 1 0 1 0 0 0
0 0 0 0 0 0 0 0 x 0 0
0 0 0 0 0 0 0 1 x 0 0
0 0 0 0 0 0 0 0 x 0 0
0 0 0 0 0 0 0 1 x 0 0
0 0 0 0 0 0 0 0 x 0 0
0 0 0 0 0 0 0 1 x 0 0
0 0 0 0 0 0 0 0 x 0 0
0 0 0 0 0 0 0 1 x 0 0
0 0 0 0 0 0 0 0 x 0 0
0 0 0 0 0 0 0 1 x 0 0
0 0 0 0 0 0 0 0 x 0 0
0 0 0 0 0 0 0 1 x 0 0
0 0 0 0 0 0 0 0 x 0 0
0 0 0 0 0 0 0 1 x 0 0
0 0 0 0 0 0 0 0 x 0 0
0 0 0 0 0 0 0 1 x 0 0
0 0 0 0 0 0 0 0 x 0 0
0 0 0 0 0 0 0 1 x 0 0
0 0 0 0 0 0 0 0 x 0 0
0 0 0 0 0 0 0 1 x 0 0
0 0 0 0 0 0 0 0 x 0 0
0 0 0 0 0 0 0 1 x 0 0
0 0 0 0 0 0 0 0 x 0 0
0 0 0 0 0 0 0 1 x 0 0
0 0 0 0 0 0 0 0 x 0 0
0 0 0 0 0 0 0 1 x 0 0
0 0 0 0 0 0 0 0 x 0 0
0 0 0 0 0 0 0 1 x 0 0
0 0 0 0 0 0 0 0 x 0 0
0 0 0 0 0 0 0 1 x 0 0
0 0 0 0 0 0 0 0 x 0 0
0 0 0 0 0 0 0 1 x 0 0
0 0 0 0 0 0 0 0 x 0 0
0 0 0 0 0 0 0 1 x 0 0
0 0 0 0 0 0 0 0 x 0 0
0 0 0 0 0 0 0 1 x 0 0
0 0 0 0 0 0 0 0 x 0 0
0 0 0 0 0 0 0 1 x 0 0
0 0 0 0 0 0 0 0 x 0 0
0 0 0 0 0 0 0 1 x 0 0
0 0 0 0 0 0 0 0 x 0 0
0 0 0 0 0 0 0 1 x 0 0
0 0 0 0 0 0 0 0 x 0 0
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*/

/* Test case 04_P03T1:
M N progIN reset progLoad start result clk valid done output
0 0 0 0 0 0 0 0 x x x
0 0 0 0 0 0 0 1 x x x
0 0 0 1 0 0 0 0 x x x
0 0 0 1 0 0 0 1 0 0 x
0 0 0 0 0 0 0 0 0 0 x
0 0 0 0 0 0 0 1 0 0 x
0 0 0 0 0 0 0 0 0 0 x
0 0 0 0 0 0 0 1 0 0 x
0 0 0 0 0 0 0 0 0 0 x
0 0 0 0 0 0 0 1 0 0 x
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*/

/* Test case 07_P06T1:
M N progIN reset progLoad start result clk valid done output
0 0 0 0 0 0 0 0 x x x
0 0 0 0 0 0 0 1 x x x
0 0 0 1 0 0 0 0 x x x
0 0 0 1 0 0 0 1 0 0 x
0 0 0 0 0 0 0 0 0 0 x
0 0 0 0 0 0 0 1 0 0 x
0 0 0 0 0 0 0 0 0 0 x
0 0 0 0 0 0 0 1 0 0 x
0 0 0 0 0 0 0 0 0 0 x
0 0 0 0 0 0 0 1 0 0 x
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*/

/* Test case 10_P06T4:
M N progIN reset progLoad start result clk valid done output
0 0 0 0 0 0 0 0 x x x
0 0 0 0 0 0 0 1 x x x
0 0 0 1 0 0 0 0 x x x
0 0 0 1 0 0 0 1 0 0 x
0 0 0 0 0 0 0 0 0 0 x
0 0 0 0 0 0 0 1 0 0 x
0 0 0 0 0 0 0 0 0 0 x
0 0 0 0 0 0 0 1 0 0 x
0 0 0 0 0 0 0 0 0 0 x
0 0 0 0 0 0 0 1 0 0 x
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*/

/* Test case testbysomeone1:
M N progIN reset progLoad start result clk valid done output					
0 0 0 0 0 0 0 0 x x x	
0 0 0 0 0 0 0 1 x x x	
0 0 0 1 0 0 0 0 x x x	
0 0 0 1 0 0 0 1 0 0 0	
0 0 0 0 0 0 0 0 0 0 0	
0 0 0 0 0 0 0 1 0 0 0	
0 0 0 0 0 0 0 0 0 0 0	
0 0 0 0 0 0 0 1 0 0 0	
0 0 0 0 0 0 0 0 0 0 0	
0 0 0 0 0 0 0 1 0 0 0	
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*/

/* Test case testbysomeone2:
M N progIN reset progLoad start result clk valid done output
0 0 0 0 0 0 0 0 x x x
0 0 0 0 0 0 0 1 x x x
0 0 0 1 0 0 0 0 x x x
0 0 0 1 0 0 0 1 0 0 0
0 0 0 0 0 0 0 0 0 0 0
0 0 0 0 0 0 0 1 0 0 0
0 0 0 0 0 0 0 0 0 0 0
0 0 0 0 0 0 0 1 0 0 0
0 0 0 0 0 0 0 0 0 0 0
0 0 0 0 0 0 0 1 0 0 0
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*/

/* Test case testbysomeone3:
M N progIN reset progLoad start result clk valid done output
0 0 0 0 0 0 0 0 x x x
0 0 0 0 0 0 0 1 x x x
0 0 0 1 0 0 0 0 x x x
0 0 0 1 0 0 0 1 0 0 0
0 0 0 0 0 0 0 0 0 0 0
0 0 0 0 0 0 0 1 0 0 0
0 0 0 0 0 0 0 0 0 0 0
0 0 0 0 0 0 0 1 0 0 0
0 0 0 0 0 0 0 0 0 0 0
0 0 0 0 0 0 0 1 0 0 0
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*/

/* Test case testbysomeone4:
M N progIN reset progLoad start result clk valid done output			
0 0 0 0 0 0 0 0 x x x
0 0 0 0 0 0 0 1 x x x
0 0 0 1 0 0 0 0 x x x
0 0 0 1 0 0 0 1 0 0 0
0 0 0 0 0 0 0 0 0 0 0
0 0 0 0 0 0 0 1 0 0 0
0 0 0 0 0 0 0 0 0 0 0
0 0 0 0 0 0 0 1 0 0 0
0 0 0 0 0 0 0 0 0 0 0
0 0 0 0 0 0 0 1 0 0 0
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*/

/* Test case testbysomeone5:
M N progIN reset progLoad start result clk valid done output
0 0 0 0 0 0 0 0 0 0 0
0 0 0 0 0 0 0 1 0 0 0
0 0 0 1 0 0 0 0 0 0 0
0 0 0 1 0 0 0 1 0 0 0
0 0 0 0 0 0 0 0 0 0 0
0 0 0 0 0 0 0 1 0 0 0
0 0 0 0 0 0 0 0 0 0 0
0 0 0 0 0 0 0 1 0 0 0
0 0 0 0 0 0 0 0 0 0 0
0 0 0 0 0 0 0 1 0 0 0
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*/

/* Test case 02_P01T02:
M N progIN reset progLoad start result clk valid done output
0 0 0 0 0 0 0 0 x x x
0 0 0 0 0 0 0 1 x x x
0 0 0 1 0 0 0 0 x x x
0 0 0 1 0 0 0 1 0 0 0
0 0 0 0 0 0 0 0 0 0 0
0 0 0 0 0 0 0 1 0 0 0
0 0 0 0 0 0 0 0 0 0 0
0 0 0 0 0 0 0 1 0 0 0
0 0 0 0 0 0 0 0 0 0 0
0 0 0 0 0 0 0 1 0 0 0
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*/

/* Test case 05_P04T1:
M N progIN reset progLoad start result clk valid done output
0 0 0 0 0 0 0 0 x x x
0 0 0 0 0 0 0 1 x x x
0 0 0 1 0 0 0 0 x x x
0 0 0 1 0 0 0 1 0 0 x
0 0 0 0 0 0 0 0 0 0 x
0 0 0 0 0 0 0 1 0 0 x
0 0 0 0 0 0 0 0 0 0 x
0 0 0 0 0 0 0 1 0 0 x
0 0 0 0 0 0 0 0 0 0 x
0 0 0 0 0 0 0 1 0 0 x
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*/

/* Test case 08_P06T2:
M N progIN reset progLoad start result clk valid done output
0 0 0 0 0 0 0 0 x x x
0 0 0 0 0 0 0 1 x x x
0 0 0 1 0 0 0 0 x x x
0 0 0 1 0 0 0 1 0 0 x
0 0 0 0 0 0 0 0 0 0 x
0 0 0 0 0 0 0 1 0 0 x
0 0 0 0 0 0 0 0 0 0 x
0 0 0 0 0 0 0 1 0 0 x
0 0 0 0 0 0 0 0 0 0 x
0 0 0 0 0 0 0 1 0 0 x
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*/

/* Test case 03_P02T01:
M N progIN reset progLoad start result clk valid done output
0 0 0 0 0 0 0 0 x x x
0 0 0 0 0 0 0 1 x x x
0 0 0 1 0 0 0 0 x x x
0 0 0 1 0 0 0 1 0 0 0
0 0 0 0 0 0 0 0 0 0 0
0 0 0 0 0 0 0 1 0 0 0
0 0 0 0 0 0 0 0 0 0 0
0 0 0 0 0 0 0 1 0 0 0
0 0 0 0 0 0 0 0 0 0 0
0 0 0 0 0 0 0 1 0 0 0
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*/

/* Test case 06_P05T1:
M N progIN reset progLoad start result clk valid done output
0 0 0 0 0 0 0 0 x x x
0 0 0 0 0 0 0 1 x x x
0 0 0 1 0 0 0 0 x x x
0 0 0 1 0 0 0 1 0 0 x
0 0 0 0 0 0 0 0 0 0 x
0 0 0 0 0 0 0 1 0 0 x
0 0 0 0 0 0 0 0 0 0 x
0 0 0 0 0 0 0 1 0 0 x
0 0 0 0 0 0 0 0 0 0 x
0 0 0 0 0 0 0 1 0 0 x
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*/

/* Test case 09_P06T3:
M N progIN reset progLoad start result clk valid done output
0 0 0 0 0 0 0 0 x x x
0 0 0 0 0 0 0 1 x x x
0 0 0 1 0 0 0 0 x x x
0 0 0 1 0 0 0 1 0 0 x
0 0 0 0 0 0 0 0 0 0 x
0 0 0 0 0 0 0 1 0 0 x
0 0 0 0 0 0 0 0 0 0 x
0 0 0 0 0 0 0 1 0 0 x
0 0 0 0 0 0 0 0 0 0 x
0 0 0 0 0 0 0 1 0 0 x
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*/

/* Test case testbyphone1:
M N progIN reset progLoad start result clk valid done output
0 0 0 0 0 0 0 0 x x x
0 0 0 0 0 0 0 1 x x x
0 0 0 1 0 0 0 0 x x x
0 0 0 1 0 0 0 1 x x x
0 0 0 0 0 0 0 0 x x x
0 0 0 0 0 0 0 1 x x x
0 0 0 0 0 0 0 0 x x x
0 0 0 0 0 0 0 1 x x x
0 0 0 0 0 0 0 0 x x x
0 0 0 0 0 0 0 1 x x x
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*/
